// Logisim project 3by8_decoder.circ as structural Verilog: 1 circuit, main circuit main
module main (
  input  in_1,
  input  in_2,
  input  in_3,
  output [7:0] out_4
);

  wire not_1_out, not_2_out, not_3_out;

  not not_1 (not_1_out, in_1);
  not not_2 (not_2_out, in_2);
  not not_3 (not_3_out, in_3);
  and and_1 (out_4[0], not_1_out, not_2_out, not_3_out);
  and and_2 (out_4[1], not_1_out, not_2_out, in_3);
  and and_3 (out_4[2], not_1_out, in_2, not_3_out);
  and and_4 (out_4[3], not_1_out, in_2, in_3);
  and and_5 (out_4[4], in_1, not_2_out, not_3_out);
  and and_6 (out_4[5], in_1, not_2_out, in_3);
  and and_7 (out_4[6], in_1, in_2, not_3_out);
  and and_8 (out_4[7], in_1, in_2, in_3);
endmodule
