// Logisim project 4bitCPU.circ as structural Verilog: 22 circuits, main circuit main
module main (
  input  [3:0] in_1,
  input  in_2,
  input  in_3,
  input  in_4,
  input  in_5,
  input  in_6,
  output out_7,
  output [3:0] out_8
);

  wire [2:0] cpu_reg_4_1_out_4;

  CPU_REG_4 cpu_reg_4_1 (.in_1(in_1), .in_2(in_2), .in_3(in_4), .out_4({out_7, cpu_reg_4_1_out_4}));
  CPU_REG_4 cpu_reg_4_2 (.in_1({cpu_reg_4_1_out_4, in_6}), .in_2(in_3), .in_3(in_5), .out_4(out_8));
endmodule

module CPU_MEM_1 (
  input  s,
  input  e,
  output q
);

  wire nand_1_out, nand_2_out, nand_4_out;

  nand nand_1 (nand_1_out, s, e);
  nand nand_2 (nand_2_out, e, nand_1_out);
  nand nand_3 (q, nand_1_out, nand_4_out);
  nand nand_4 (nand_4_out, q, nand_2_out);

  // Notes on the sheet:
  //   1 bit memory cell
endmodule

module CPU_MEM_4 (
  input  [3:0] in_1,
  input  in_2,
  output [3:0] out_3
);

  CPU_MEM_1 cpu_mem_1_1 (.s(in_1[0]), .e(in_2), .q(out_3[0]));
  CPU_MEM_1 cpu_mem_1_2 (.s(in_1[1]), .e(in_2), .q(out_3[1]));
  CPU_MEM_1 cpu_mem_1_3 (.s(in_1[2]), .e(in_2), .q(out_3[2]));
  CPU_MEM_1 cpu_mem_1_4 (.s(in_1[3]), .e(in_2), .q(out_3[3]));
endmodule

module CPU_REG_4 (
  input  [3:0] in_1,
  input  in_2,
  input  in_3,
  output [3:0] out_4
);

  wire [3:0] cpu_mem_4_1_out_3;

  CPU_MEM_4 cpu_mem_4_1 (.in_1(in_1), .in_2(in_2), .out_3(cpu_mem_4_1_out_3));
  CPU_ENABLE_4 cpu_enable_4_1 (.out_3(out_4));  // open: in_1, in_2
endmodule

module CPU_ENABLE_4 (
  input  [3:0] in_1,
  input  in_2,
  output [3:0] out_3
);

  and and_1 (out_3[0], in_1[0], in_2);
  and and_2 (out_3[1], in_1[1], in_2);
  and and_3 (out_3[2], in_1[2], in_2);
  and and_4 (out_3[3], in_1[3], in_2);
endmodule

module HalfAdder (
  input  in_1,
  input  in_2,
  output out_3,
  output out_4
);

  xor xor_1 (out_3, in_1, in_2);
  and and_1 (out_4, in_2, in_1);
endmodule

module FullAdder (
  input  in_1,
  input  in_2,
  input  in_3,
  output out_4,
  output out_5
);

  wire halfadder_1_out_3, halfadder_1_out_4, halfadder_2_out_4;

  HalfAdder halfadder_1 (.in_1(in_1), .in_2(in_2), .out_3(halfadder_1_out_3), .out_4(halfadder_1_out_4));
  HalfAdder halfadder_2 (.in_1(in_3), .in_2(halfadder_1_out_3), .out_3(out_4), .out_4(halfadder_2_out_4));
  or or_1 (out_5, halfadder_2_out_4, halfadder_1_out_4);
endmodule

module Adder4b (
  input  [3:0] in_1,
  input  in_2,
  input  [3:0] in_3,
  output out_4,
  output [3:0] out_5
);

  wire fulladder_2_out_5, fulladder_3_out_5, fulladder_4_out_5;

  FullAdder fulladder_1 (.in_1(in_1[3]), .in_2(in_3[3]), .in_3(fulladder_2_out_5), .out_5(out_4), .out_4(out_5[3]));
  FullAdder fulladder_2 (
    .in_1(in_1[2]), .in_2(in_3[2]), .in_3(fulladder_3_out_5), .out_5(fulladder_2_out_5), .out_4(out_5[2]));
  FullAdder fulladder_3 (
    .in_1(in_1[1]), .in_2(in_3[1]), .in_3(fulladder_4_out_5), .out_5(fulladder_3_out_5), .out_4(out_5[1]));
  FullAdder fulladder_4 (.in_1(in_1[0]), .in_2(in_3[0]), .in_3(in_2), .out_5(fulladder_4_out_5), .out_4(out_5[0]));
endmodule

module Decoder4x16 (
  input  a,
  input  b,
  input  c,
  input  d,
  output o1,
  output o2,
  output o3,
  output o4,
  output o5,
  output o6,
  output o7,
  output o8,
  output o9,
  output o10,
  output o11,
  output o12,
  output o13,
  output o14,
  output o15,
  output o16
);

  wire not_1_out, not_2_out, not_3_out, not_4_out;

  not not_1 (not_1_out, a);
  not not_2 (not_2_out, b);
  not not_3 (not_3_out, c);
  not not_4 (not_4_out, d);
  and and_1 (o1, a, b, c, d);
  and and_2 (o2, a, b, c, not_4_out);
  and and_3 (o3, a, b, not_3_out, d);
  and and_4 (o4, a, b, not_3_out, not_4_out);
  and and_5 (o5, a, not_2_out, c, d);
  and and_6 (o6, a, not_2_out, c, not_4_out);
  and and_7 (o7, a, not_2_out, not_3_out, d);
  and and_8 (o8, a, not_2_out, not_3_out, not_4_out);
  and and_9 (o9, not_1_out, b, c, d);
  and and_10 (o10, not_1_out, b, c, not_4_out);
  and and_11 (o11, not_1_out, b, not_3_out, d);
  and and_12 (o12, not_1_out, b, not_3_out, not_4_out);
  and and_13 (o13, not_1_out, not_2_out, c, d);
  and and_14 (o14, not_1_out, not_2_out, c, not_4_out);
  and and_15 (o15, not_1_out, not_2_out, not_3_out, d);
  and and_16 (o16, not_1_out, not_2_out, not_3_out, not_4_out);
endmodule

module SHR4bit (
  input  [3:0] in_1,
  input  in_2,
  output out_3,
  output [3:0] out_4
);

  wire [3:1] cpu_reg_4_1_out_4;

  CPU_REG_4 cpu_reg_4_1 (.in_1(in_1), .in_2(1'b1), .in_3(1'b1), .out_4({cpu_reg_4_1_out_4, out_3}));
  CPU_REG_4 cpu_reg_4_2 (.in_1({in_2, cpu_reg_4_1_out_4}), .in_2(1'b1), .in_3(1'b1), .out_4(out_4));
endmodule

module SHL4bit (
  input  [3:0] in_1,
  input  in_2,
  output out_3,
  output [3:0] out_4
);

  wire [2:0] cpu_reg_4_1_out_4;

  CPU_REG_4 cpu_reg_4_1 (.in_1(in_1), .in_2(1'b1), .in_3(1'b1), .out_4({out_3, cpu_reg_4_1_out_4}));
  CPU_REG_4 cpu_reg_4_2 (.in_1({cpu_reg_4_1_out_4, in_2}), .in_2(1'b1), .in_3(1'b1), .out_4(out_4));
endmodule

module Not4bit (
  input  [3:0] in_1,
  output [3:0] out_2
);

  not not_1 (out_2[3], in_1[3]);
  not not_2 (out_2[2], in_1[2]);
  not not_3 (out_2[1], in_1[1]);
  not not_4 (out_2[0], in_1[0]);
endmodule

module And4bit (
  input  [3:0] in_1,
  input  [3:0] in_2,
  output [3:0] out_3
);

  and and_1 (out_3[3], in_1[3], in_2[3]);
  and and_2 (out_3[2], in_1[2], in_2[2]);
  and and_3 (out_3[1], in_1[1], in_2[1]);
  and and_4 (out_3[0], in_1[0], in_2[0]);
endmodule

module Or4bit (
  input  [3:0] in_1,
  input  [3:0] in_2,
  output [3:0] out_3
);

  or or_1 (out_3[3], in_1[3], in_2[3]);
  or or_2 (out_3[2], in_1[2], in_2[2]);
  or or_3 (out_3[1], in_1[1], in_2[1]);
  or or_4 (out_3[0], in_1[0], in_2[0]);
endmodule

module XorLE1bit (
  input  a,
  input  b,
  input  a_larger,
  input  ab_eq,
  output out_5,
  output a_larger_2,
  output equal
);

  wire and_2_out, not_1_out;

  xor xor_1 (out_5, a, b);
  not not_1 (not_1_out, out_5);
  and and_1 (equal, ab_eq, not_1_out);
  and and_2 (and_2_out, ab_eq, a, out_5);
  or or_1 (a_larger_2, and_2_out, a_larger);
endmodule

module Zero4bit (
  input  [3:0] in_1,
  output out_2
);

  wire or_1_out;

  or or_1 (or_1_out, in_1[3], in_1[2], in_1[1], in_1[0]);
  not not_1 (out_2, or_1_out);
endmodule

module Xor4bit (
  input  [3:0] in_1,
  input  [3:0] in_2,
  output [3:0] out_3,
  output larger,
  output equal
);

  wire xorle1bit_1_a_larger_2, xorle1bit_1_equal, xorle1bit_2_a_larger_2, xorle1bit_2_equal,
       xorle1bit_3_a_larger_2, xorle1bit_3_equal;

  XorLE1bit xorle1bit_1 (
    .a(in_1[0]), .b(in_2[0]), .ab_eq(1'b1), .a_larger(1'b0), .out_5(out_3[0]), .equal(xorle1bit_1_equal),
    .a_larger_2(xorle1bit_1_a_larger_2));
  XorLE1bit xorle1bit_2 (
    .a(in_1[1]), .b(in_2[1]), .ab_eq(xorle1bit_1_equal), .a_larger(xorle1bit_1_a_larger_2), .out_5(out_3[1]),
    .equal(xorle1bit_2_equal), .a_larger_2(xorle1bit_2_a_larger_2));
  XorLE1bit xorle1bit_3 (
    .a(in_1[2]), .b(in_2[2]), .ab_eq(xorle1bit_2_equal), .a_larger(xorle1bit_2_a_larger_2), .out_5(out_3[2]),
    .equal(xorle1bit_3_equal), .a_larger_2(xorle1bit_3_a_larger_2));
  XorLE1bit xorle1bit_4 (
    .a(in_1[3]), .b(in_2[3]), .ab_eq(xorle1bit_3_equal), .a_larger(xorle1bit_3_a_larger_2), .out_5(out_3[3]),
    .equal(equal), .a_larger_2(larger));
endmodule

module ALU4bit (
  input  carry_in,
  input  [3:0] in_2,
  input  [3:0] in_3,
  input  c,
  input  b,
  input  a,
  output out_7,
  output [3:0] out_8,
  output carry_out,
  output larger,
  output equal
);

  wire adder4b_1_out_4, decoder3x8_1_o2, decoder3x8_1_o3, decoder3x8_1_o4, decoder3x8_1_o5, decoder3x8_1_o6,
       decoder3x8_1_o7, decoder3x8_1_o8, shl4bit_1_out_3, shr4bit_1_out_3;
  wire [3:0] adder4b_1_out_5, and4bit_1_out_3, not4bit_1_out_2, or4bit_1_out_3, shl4bit_1_out_4,
       shr4bit_1_out_4, xor4bit_1_out_3;

  Not4bit not4bit_1 (.in_1(in_2), .out_2(not4bit_1_out_2));
  SHL4bit shl4bit_1 (.in_2(carry_in), .in_1(in_2), .out_3(shl4bit_1_out_3), .out_4(shl4bit_1_out_4));
  SHR4bit shr4bit_1 (.in_2(carry_in), .in_1(in_2), .out_3(shr4bit_1_out_3), .out_4(shr4bit_1_out_4));
  Or4bit or4bit_1 (.in_1(in_2), .in_2(in_3), .out_3(or4bit_1_out_3));
  And4bit and4bit_1 (.in_1(in_2), .in_2(in_3), .out_3(and4bit_1_out_3));
  Adder4b adder4b_1 (.in_1(in_2), .in_3(in_3), .in_2(carry_in), .out_4(adder4b_1_out_4), .out_5(adder4b_1_out_5));
  Xor4bit xor4bit_1 (.in_2(in_3), .in_1(in_2), .larger(larger), .equal(equal), .out_3(xor4bit_1_out_3));
  Decoder3x8 decoder3x8_1 (
    .b(c), .c(b), .d(a), .o2(decoder3x8_1_o2), .o3(decoder3x8_1_o3), .o4(decoder3x8_1_o4),
    .o5(decoder3x8_1_o5), .o6(decoder3x8_1_o6), .o7(decoder3x8_1_o7), .o8(decoder3x8_1_o8));  // open: o1
  and and_1 (carry_out, shl4bit_1_out_3, decoder3x8_1_o6);
  and and_2 (carry_out, shr4bit_1_out_3, decoder3x8_1_o7);
  and and_3 (carry_out, adder4b_1_out_4, decoder3x8_1_o8);
  Controll4bit controll4bit_1 (.in_1(not4bit_1_out_2), .in_2(decoder3x8_1_o5), .out_3(out_8));
  Controll4bit controll4bit_2 (.in_1(shl4bit_1_out_4), .in_2(decoder3x8_1_o6), .out_3(out_8));
  Controll4bit controll4bit_3 (.in_1(shr4bit_1_out_4), .in_2(decoder3x8_1_o7), .out_3(out_8));
  Controll4bit controll4bit_4 (.in_1(or4bit_1_out_3), .in_2(decoder3x8_1_o3), .out_3(out_8));
  Controll4bit controll4bit_5 (.in_1(and4bit_1_out_3), .in_2(decoder3x8_1_o4), .out_3(out_8));
  Controll4bit controll4bit_6 (.in_1(adder4b_1_out_5), .in_2(decoder3x8_1_o8), .out_3(out_8));
  Controll4bit controll4bit_7 (.in_1(xor4bit_1_out_3), .in_2(decoder3x8_1_o2), .out_3(out_8));
  Zero4bit zero4bit_1 (.in_1(out_8), .out_2(out_7));
endmodule

module Decoder3x8 (
  input  b,
  input  c,
  input  d,
  output o1,
  output o2,
  output o3,
  output o4,
  output o5,
  output o6,
  output o7,
  output o8
);

  wire not_1_out, not_2_out, not_3_out;

  not not_1 (not_1_out, b);
  not not_2 (not_2_out, c);
  not not_3 (not_3_out, d);
  and and_1 (o1, b, c, d);
  and and_2 (o2, b, c, not_3_out);
  and and_3 (o3, b, not_2_out, d);
  and and_4 (o4, b, not_2_out, not_3_out);
  and and_5 (o5, not_1_out, c, d);
  and and_6 (o6, not_1_out, c, not_3_out);
  and and_7 (o7, not_1_out, not_2_out, d);
  and and_8 (o8, not_1_out, not_2_out, not_3_out);
endmodule

module Controll4bit (
  input  [3:0] in_1,
  input  in_2,
  output [3:0] out_3
);

  wire and_1_out, and_2_out, and_3_out, and_4_out;

  and and_1 (and_1_out, in_1[0], in_2);
  and and_2 (and_2_out, in_1[1], in_2);
  and and_3 (and_3_out, in_1[2], in_2);
  and and_4 (and_4_out, in_1[3], in_2);
  assign out_3[0] = in_2 ? and_1_out : 1'bz;  // Controlled_Buffer controlled_buffer_1
  assign out_3[1] = in_2 ? and_2_out : 1'bz;  // Controlled_Buffer controlled_buffer_2
  assign out_3[2] = in_2 ? and_3_out : 1'bz;  // Controlled_Buffer controlled_buffer_3
  assign out_3[3] = in_2 ? and_4_out : 1'bz;  // Controlled_Buffer controlled_buffer_4
endmodule

module Clock4bit (
  input  in_1,
  output clk,
  output clks,
  output clke
);

  wire j_k_ff_1_qn, nand_1_out;

  J_K_Flip_Flop j_k_ff_1 (.J(1'b1), .K(1'b1), .clk(in_1), .Q(clk), .Qn(j_k_ff_1_qn));  // open: preset, reset
  nand nand_1 (nand_1_out, in_1, clk);
  nand nand_2 (clke, j_k_ff_1_qn, in_1);
  not not_1 (clks, nand_1_out);
endmodule

module Stepper (
  input  in_1,
  input  in_2,
  output out_3,
  output out_4,
  output out_5,
  output out_6,
  output out_7
);

  wire cpu_mem_1_1_q, cpu_mem_1_2_q, cpu_mem_1_3_q, cpu_mem_1_4_q, cpu_mem_1_5_q, cpu_mem_1_6_q,
       cpu_mem_1_7_q, not_1_out, not_2_out, not_3_out, not_4_out, not_5_out, not_6_out, or_1_out, or_3_out;

  not not_1 (not_1_out, in_1);
  not not_2 (not_2_out, in_2);
  or or_1 (or_1_out, in_1, in_2);
  or or_2 (out_3, in_1, not_3_out);
  CPU_MEM_1 cpu_mem_1_1 (.s(not_1_out), .e(or_3_out), .q(cpu_mem_1_1_q));
  or or_3 (or_3_out, in_1, not_2_out);
  not not_3 (not_3_out, cpu_mem_1_2_q);
  CPU_MEM_1 cpu_mem_1_2 (.s(cpu_mem_1_1_q), .e(or_1_out), .q(cpu_mem_1_2_q));
  and and_1 (out_4, cpu_mem_1_2_q, not_4_out);
  CPU_MEM_1 cpu_mem_1_3 (.s(cpu_mem_1_2_q), .e(or_3_out), .q(cpu_mem_1_3_q));
  not not_4 (not_4_out, cpu_mem_1_4_q);
  CPU_MEM_1 cpu_mem_1_4 (.s(cpu_mem_1_3_q), .e(or_1_out), .q(cpu_mem_1_4_q));
  and and_2 (out_5, cpu_mem_1_4_q, not_5_out);
  CPU_MEM_1 cpu_mem_1_5 (.s(cpu_mem_1_4_q), .e(or_3_out), .q(cpu_mem_1_5_q));
  not not_5 (not_5_out, cpu_mem_1_6_q);
  CPU_MEM_1 cpu_mem_1_6 (.s(cpu_mem_1_5_q), .e(or_1_out), .q(cpu_mem_1_6_q));
  CPU_MEM_1 cpu_mem_1_7 (.s(cpu_mem_1_6_q), .e(or_1_out), .q(cpu_mem_1_7_q));
  and and_3 (out_6, cpu_mem_1_6_q, not_6_out);
  not not_6 (not_6_out, out_7);
  CPU_MEM_1 cpu_mem_1_8 (.s(cpu_mem_1_7_q), .e(or_3_out), .q(out_7));
endmodule
