// Logisim project 4bitMem.circ as structural Verilog
module CPU_MEM_1 (
  input  s,
  input  e,
  output q
);

  wire nand_1_out, nand_2_out, nand_4_out;

  nand nand_1 (nand_1_out, s, e);
  nand nand_2 (nand_2_out, e, nand_1_out);
  nand nand_3 (q, nand_1_out, nand_4_out);
  nand nand_4 (nand_4_out, q, nand_2_out);

  // Notes on the sheet:
  //   1 bit memory cell
endmodule

module CPU_MEM_4 (
  input  [3:0] in_1,
  input  in_2,
  output [3:0] out_3
);

  CPU_MEM_1 cpu_mem_1_1 (.s(in_1[0]), .e(in_2), .q(out_3[0]));
  CPU_MEM_1 cpu_mem_1_2 (.s(in_1[1]), .e(in_2), .q(out_3[1]));
  CPU_MEM_1 cpu_mem_1_3 (.s(in_1[2]), .e(in_2), .q(out_3[2]));
  CPU_MEM_1 cpu_mem_1_4 (.s(in_1[3]), .e(in_2), .q(out_3[3]));
endmodule

module CPU_REG_4 (
  input  [3:0] in_1,
  input  in_2,
  input  in_3,
  output [3:0] out_4
);

  wire [3:0] cpu_mem_4_1_out_3;

  CPU_MEM_4 cpu_mem_4_1 (.in_1(in_1), .in_2(in_2), .out_3(cpu_mem_4_1_out_3));
  CPU_ENABLE_4 cpu_enable_4_1 (.in_1(cpu_mem_4_1_out_3), .in_2(in_3), .out_3(out_4));
endmodule

module CPU_ENABLE_4 (
  input  [3:0] in_1,
  input  in_2,
  output [3:0] out_3
);

  and and_1 (out_3[0], in_1[0], in_2);
  and and_2 (out_3[1], in_1[1], in_2);
  and and_3 (out_3[2], in_1[2], in_2);
  and and_4 (out_3[3], in_1[3], in_2);
endmodule
