// Logisim project 4by16decoder.circ as structural Verilog: 1 circuit, main circuit main
module main (
  input  a,
  input  b,
  input  c,
  input  d,
  output o1,
  output o2,
  output o3,
  output o4,
  output o5,
  output o6,
  output o7,
  output o8,
  output o9,
  output o10,
  output o11,
  output o12,
  output o13,
  output o14,
  output o15,
  output o16
);

  wire not_1_out, not_2_out, not_3_out, not_4_out;

  not not_1 (not_1_out, a);
  not not_2 (not_2_out, b);
  not not_3 (not_3_out, c);
  not not_4 (not_4_out, d);
  and and_1 (o1, a, b, c, d);
  and and_2 (o2, a, b, c, not_4_out);
  and and_3 (o3, a, b, not_3_out, d);
  and and_4 (o4, a, b, not_3_out, not_4_out);
  and and_5 (o5, a, not_2_out, c, d);
  and and_6 (o6, a, not_2_out, c, not_4_out);
  and and_7 (o7, a, not_2_out, not_3_out, d);
  and and_8 (o8, a, not_2_out, not_3_out, not_4_out);
  and and_9 (o9, not_1_out, b, c, d);
  and and_10 (o10, not_1_out, b, c, not_4_out);
  and and_11 (o11, not_1_out, b, not_3_out, d);
  and and_12 (o12, not_1_out, b, not_3_out, not_4_out);
  and and_13 (o13, not_1_out, not_2_out, c, d);
  and and_14 (o14, not_1_out, not_2_out, c, not_4_out);
  and and_15 (o15, not_1_out, not_2_out, not_3_out, d);
  and and_16 (o16, not_1_out, not_2_out, not_3_out, not_4_out);
endmodule
