// Logisim project Adders.circ as structural Verilog: 4 circuits, main circuit main
module main (
  input  [3:0] in_1,
  input  in_2,
  input  [3:0] in_3,
  output out_4,
  output [3:0] out_5
);

  wire fulladder_2_out_5, fulladder_3_out_5, fulladder_4_out_5;

  FullAdder fulladder_1 (.in_1(in_1[3]), .in_2(in_3[3]), .in_3(fulladder_2_out_5), .out_5(out_4), .out_4(out_5[3]));
  FullAdder fulladder_2 (
    .in_1(in_1[2]), .in_2(in_3[2]), .in_3(fulladder_3_out_5), .out_5(fulladder_2_out_5), .out_4(out_5[2]));
  FullAdder fulladder_3 (
    .in_1(in_1[1]), .in_2(in_3[1]), .in_3(fulladder_4_out_5), .out_5(fulladder_3_out_5), .out_4(out_5[1]));
  FullAdder fulladder_4 (.in_1(in_1[0]), .in_2(in_3[0]), .in_3(in_2), .out_5(fulladder_4_out_5), .out_4(out_5[0]));
endmodule

module HalfAdder (
  input  in_1,
  input  in_2,
  output out_3,
  output out_4
);

  xor xor_1 (out_3, in_1, in_2);
  and and_1 (out_4, in_2, in_1);
endmodule

module FullAdder (
  input  in_1,
  input  in_2,
  input  in_3,
  output out_4,
  output out_5
);

  wire halfadder_1_out_3, halfadder_1_out_4, halfadder_2_out_4;

  HalfAdder halfadder_1 (.in_1(in_1), .in_2(in_2), .out_3(halfadder_1_out_3), .out_4(halfadder_1_out_4));
  HalfAdder halfadder_2 (.in_1(in_3), .in_2(halfadder_1_out_3), .out_3(out_4), .out_4(halfadder_2_out_4));
  or or_1 (out_5, halfadder_2_out_4, halfadder_1_out_4);
endmodule

module Adder4b (
  input  [3:0] in_1,
  input  in_2,
  input  [3:0] in_3,
  output out_4,
  output [3:0] out_5
);

  wire fulladder_2_out_5, fulladder_3_out_5, fulladder_4_out_5;

  FullAdder fulladder_1 (.in_1(in_1[3]), .in_2(in_3[3]), .in_3(fulladder_2_out_5), .out_5(out_4), .out_4(out_5[3]));
  FullAdder fulladder_2 (
    .in_1(in_1[2]), .in_2(in_3[2]), .in_3(fulladder_3_out_5), .out_5(fulladder_2_out_5), .out_4(out_5[2]));
  FullAdder fulladder_3 (
    .in_1(in_1[1]), .in_2(in_3[1]), .in_3(fulladder_4_out_5), .out_5(fulladder_3_out_5), .out_4(out_5[1]));
  FullAdder fulladder_4 (.in_1(in_1[0]), .in_2(in_3[0]), .in_3(in_2), .out_5(fulladder_4_out_5), .out_4(out_5[0]));
endmodule
