// Logisim project CPU_DESIGN.circ as structural Verilog: 40 circuits, main circuit main
module main (
);


  // Notes on the sheet:
  //   simulation. HAVE FUN !!!
  //   Welcome to the course. If you have just
  //   started then click on the CPU_MEM_1 block
  //   on the top left of the screen to run your first
endmodule

module CPU_MEM_1 (
  input  in_1,
  input  in_2,
  output out_3
);

  wire nand_1_out, nand_2_out, nand_4_out;

  nand nand_1 (nand_1_out, in_1, in_2);
  nand nand_2 (nand_2_out, nand_1_out, in_2);
  nand nand_3 (out_3, nand_1_out, nand_4_out);
  nand nand_4 (nand_4_out, out_3, nand_2_out);

  // Notes on the sheet:
  //   in_2: pull=down
  //   in_1: pull=down
endmodule

module CPU_MEM_8 (
  input  [7:0] in_1,
  input  s,
  output [7:0] out_3
);

  CPU_MEM_1 cpu_mem_1_1 (.in_2(s), .in_1(in_1[0]), .out_3(out_3[0]));
  CPU_MEM_1 cpu_mem_1_2 (.in_2(s), .in_1(in_1[1]), .out_3(out_3[1]));
  CPU_MEM_1 cpu_mem_1_3 (.in_2(s), .in_1(in_1[2]), .out_3(out_3[2]));
  CPU_MEM_1 cpu_mem_1_4 (.in_2(s), .in_1(in_1[3]), .out_3(out_3[3]));
  CPU_MEM_1 cpu_mem_1_5 (.in_2(s), .in_1(in_1[4]), .out_3(out_3[4]));
  CPU_MEM_1 cpu_mem_1_6 (.in_2(s), .in_1(in_1[5]), .out_3(out_3[5]));
  CPU_MEM_1 cpu_mem_1_7 (.in_2(s), .in_1(in_1[6]), .out_3(out_3[6]));
  CPU_MEM_1 cpu_mem_1_8 (.in_2(s), .in_1(in_1[7]), .out_3(out_3[7]));

  // Notes on the sheet:
  //   in_1: pull=down
  //   s: pull=down
  //   out_3: pull=down
endmodule

module CPU_ENABLE_8 (
  input  [7:0] in_1,
  input  in_2,
  output [7:0] out_3
);

  wire and_1_out, and_2_out, and_3_out, and_4_out, and_5_out, and_6_out, and_7_out, and_8_out;

  and and_1 (and_1_out, in_1[0], in_2);
  assign out_3[0] = in_2 ? and_1_out : 1'bz;  // Controlled_Buffer controlled_buffer_1
  and and_2 (and_2_out, in_1[1], in_2);
  assign out_3[1] = in_2 ? and_2_out : 1'bz;  // Controlled_Buffer controlled_buffer_2
  and and_3 (and_3_out, in_1[2], in_2);
  assign out_3[2] = in_2 ? and_3_out : 1'bz;  // Controlled_Buffer controlled_buffer_3
  and and_4 (and_4_out, in_1[3], in_2);
  assign out_3[3] = in_2 ? and_4_out : 1'bz;  // Controlled_Buffer controlled_buffer_4
  and and_5 (and_5_out, in_1[4], in_2);
  assign out_3[4] = in_2 ? and_5_out : 1'bz;  // Controlled_Buffer controlled_buffer_5
  and and_6 (and_6_out, in_1[5], in_2);
  assign out_3[5] = in_2 ? and_6_out : 1'bz;  // Controlled_Buffer controlled_buffer_6
  and and_7 (and_7_out, in_1[6], in_2);
  assign out_3[6] = in_2 ? and_7_out : 1'bz;  // Controlled_Buffer controlled_buffer_7
  and and_8 (and_8_out, in_1[7], in_2);
  assign out_3[7] = in_2 ? and_8_out : 1'bz;  // Controlled_Buffer controlled_buffer_8
endmodule

module CPU_REGISTER_8 (
  input  [7:0] i,
  input  s,
  input  e,
  output [7:0] REG,
  output [7:0] L_0_0718cde6
);

  wire [7:0] cpu_enable_8_1_out_3;

  CPU_MEM_8 cpu_mem_8_1 (.in_1(i), .s(s), .out_3(REG));
  CPU_ENABLE_8 cpu_enable_8_1 (.in_1(REG), .in_2(e), .out_3(cpu_enable_8_1_out_3));
  assign L_0_0718cde6 = e ? cpu_enable_8_1_out_3 : 8'bz;  // Controlled_Buffer controlled_buffer_1

  // Notes on the sheet:
  //   i: pull=down
  //   s: pull=down
  //   e: pull=down
  //   L_0_0718cde6: pull=down
endmodule

module CPU_DECODER_4x16 (
  input  [3:0] in_1,
  output L,
  output out_3,
  output out_4,
  output out_5,
  output out_6,
  output out_7,
  output out_8,
  output out_9,
  output out_10,
  output out_11,
  output out_12,
  output out_13,
  output out_14,
  output out_15,
  output out_16,
  output M
);

  wire not_1_out, not_2_out, not_3_out, not_4_out;

  not not_1 (not_1_out, in_1[0]);
  not not_2 (not_2_out, in_1[1]);
  not not_3 (not_3_out, in_1[2]);
  not not_4 (not_4_out, in_1[3]);
  and and_1 (L, not_4_out, not_3_out, not_2_out, not_1_out);
  and and_2 (out_3, not_4_out, not_3_out, not_2_out, in_1[0]);
  and and_3 (out_4, not_4_out, not_3_out, in_1[1], not_1_out);
  and and_4 (out_5, not_4_out, not_3_out, in_1[1], in_1[0]);
  and and_5 (out_6, not_4_out, in_1[2], not_2_out, not_1_out);
  and and_6 (out_7, not_4_out, in_1[2], not_2_out, in_1[0]);
  and and_7 (out_8, not_4_out, in_1[2], in_1[1], not_1_out);
  and and_8 (out_9, not_4_out, in_1[2], in_1[1], in_1[0]);
  and and_9 (out_10, in_1[3], not_3_out, not_2_out, not_1_out);
  and and_10 (out_11, in_1[3], not_3_out, not_2_out, in_1[0]);
  and and_11 (out_12, in_1[3], not_3_out, in_1[1], not_1_out);
  and and_12 (out_13, in_1[3], not_3_out, in_1[1], in_1[0]);
  and and_13 (out_14, in_1[3], in_1[2], not_2_out, not_1_out);
  and and_14 (out_15, in_1[3], in_1[2], not_2_out, in_1[0]);
  and and_15 (out_16, in_1[3], in_1[2], in_1[1], not_1_out);
  and and_16 (M, in_1[3], in_1[2], in_1[1], in_1[0]);

  // Notes on the sheet:
  //   out_13: pull=down
  //   out_14: pull=down
  //   out_15: pull=down
  //   out_16: pull=down
  //   M: pull=down
  //   L: pull=down
  //   out_3: pull=down
  //   out_4: pull=down
  //   out_5: pull=down
  //   out_6: pull=down
  //   out_7: pull=down
  //   out_8: pull=down
  //   out_9: pull=down
  //   out_10: pull=down
  //   out_11: pull=down
  //   out_12: pull=down
  //   in_1: pull=down
endmodule

module CPU_REG_BYTE (
  input  [7:0] i,
  input  RESET,
  input  h,
  input  v,
  input  s,
  input  e,
  output [7:0] o,
  output [7:0] op
);

  wire and_1_out, and_2_out, and_3_out, or_1_out;
  wire [7:0] cpu_register_8_1_l_0_0718cde6;

  and and_1 (and_1_out, h, v);
  and and_2 (and_2_out, and_1_out, s);
  and and_3 (and_3_out, and_1_out, e);
  or or_1 (or_1_out, RESET, and_2_out);
  CPU_REGISTER_8 cpu_register_8_1 (
    .i(i), .s(or_1_out), .e(and_3_out), .REG(op), .L_0_0718cde6(cpu_register_8_1_l_0_0718cde6));
  assign o = and_3_out ? cpu_register_8_1_l_0_0718cde6 : 8'bz;  // Controlled_Buffer controlled_buffer_1

  // Notes on the sheet:
  //   h: pull=down
  //   v: pull=down
  //   s: pull=down
  //   e: pull=down
  //   op: pull=down
  //   RESET: pull=down
  //   i: pull=down
  //   o: pull=down
endmodule

module CPU_RAM_256 (
  input  reset,
  input  [7:0] i,
  input  sa,
  input  [7:0] address,
  input  s,
  input  e,
  output [7:0] o,
  output [7:0] L_15_49b3f215,
  output [7:0] L_14_09a57ae2,
  output [7:0] L_13_b05b92d5,
  output [7:0] L_12_d8925d08,
  output [7:0] L_11_d9827db8,
  output [7:0] L_10_884b6e1b,
  output [7:0] L_9_e63877d4,
  output [7:0] L_8_0263bcbb,
  output [7:0] L_7_21e06148,
  output [7:0] L_6_35fe27e4,
  output [7:0] L_5_5a09c7b9,
  output [7:0] L_4_df9eb970,
  output [7:0] out_20,
  output [7:0] L_2_021c411d,
  output [7:0] L_1_a0dbb3e4,
  output [7:0] L_0_0718cde6,
  output [7:0] L_31_244d0c43,
  output [7:0] L_30_8aab3891,
  output [7:0] L_29_20ac879c,
  output [7:0] L_28_887e6408,
  output [7:0] L_27_6ee616b1,
  output [7:0] L_26_60793931,
  output [7:0] L_25_edd3a926,
  output [7:0] L_24_60803382,
  output [7:0] L_23_5bebf840,
  output [7:0] L_22_3fa04d94,
  output [7:0] L_21_2793d292,
  output [7:0] L_20_b0f18e1f,
  output [7:0] L_19_df0ab950,
  output [7:0] L_18_77c23569,
  output [7:0] L_17_a6f2001c,
  output [7:0] L_16_4a4ef9fa,
  output [7:0] L_47_4b05a2a0,
  output [7:0] L_46_1b94c33f,
  output [7:0] L_45_4e81981e,
  output [7:0] L_44_455ab579,
  output [7:0] L_43_5cd73d77,
  output [7:0] L_42_4597cfe2,
  output [7:0] L_41_1d3782fe,
  output [7:0] L_40_4ca6ce3b,
  output [7:0] L_39_a919e418,
  output [7:0] L_38_9f366372,
  output [7:0] L_37_b49ff5fb,
  output [7:0] L_36_5c9707bd,
  output [7:0] L_35_a8d555d1,
  output [7:0] L_34_198975c3,
  output [7:0] L_33_b87346dc,
  output [7:0] L_32_b3d84c07,
  output [7:0] L_63_9b5c08e1,
  output [7:0] L_62_d1b1203b,
  output [7:0] L_61_c72da5da,
  output [7:0] L_60_007aac1b,
  output [7:0] L_59_5187825b,
  output [7:0] L_58_cc0e5230,
  output [7:0] L_57_b8cf3fac,
  output [7:0] L_56_a274d823,
  output [7:0] L_55_09b2a5b5,
  output [7:0] L_54_7adb3ac6,
  output [7:0] L_53_e0194783,
  output [7:0] L_52_39705d0b,
  output [7:0] L_51_8e7c53d8,
  output [7:0] L_50_30e7a076,
  output [7:0] L_49_9d69905f,
  output [7:0] L_48_cd210754,
  output [7:0] L_79_65da426e,
  output [7:0] L_78_c15dfd7a,
  output [7:0] L_77_c0c0c278,
  output [7:0] L_76_0dd232d6,
  output [7:0] L_75_6762c5d7,
  output [7:0] L_74_b7af5351,
  output [7:0] L_73_dfdb2ca0,
  output [7:0] L_72_0f3ff63b,
  output [7:0] L_71_7a7bc430,
  output [7:0] L_70_4c14f7ed,
  output [7:0] L_69_b6eb8b05,
  output [7:0] L_68_24398868,
  output [7:0] L_67_7dd7fcd5,
  output [7:0] L_66_c6e314cf,
  output [7:0] L_65_f777b26e,
  output [7:0] L_64_38ccf0ea,
  output [7:0] L_95_ef83c9fc,
  output [7:0] L_94_e033720c,
  output [7:0] L_93_734946e0,
  output [7:0] L_92_92986eb9,
  output [7:0] L_91_e4fec703,
  output [7:0] L_90_87ff629e,
  output [7:0] L_89_379e7e7e,
  output [7:0] L_88_441b4085,
  output [7:0] L_87_afa8acd5,
  output [7:0] L_86_50a3a49b,
  output [7:0] L_85_e1dcb90a,
  output [7:0] L_84_7571b0a3,
  output [7:0] L_83_0ffa05ff,
  output [7:0] L_82_f95cee65,
  output [7:0] L_81_192bbbc9,
  output [7:0] L_80_f25c8b42,
  output [7:0] L_111_5b0b1347,
  output [7:0] L_110_5061371d,
  output [7:0] L_109_49389abb,
  output [7:0] L_108_0c1b67c6,
  output [7:0] L_107_afc376ab,
  output [7:0] L_106_890633e3,
  output [7:0] L_105_ec1bd0aa,
  output [7:0] L_104_9a2c499d,
  output [7:0] L_103_4ca9a9e8,
  output [7:0] L_102_dee4d37a,
  output [7:0] L_101_4b0585e7,
  output [7:0] L_100_8c031f7c,
  output [7:0] L_99_754ffd2e,
  output [7:0] L_98_4126bf5f,
  output [7:0] L_97_edb68727,
  output [7:0] L_96_b42dc9a0,
  output [7:0] L_127_603c7aaf,
  output [7:0] L_126_ab782779,
  output [7:0] L_125_d87b9d02,
  output [7:0] L_124_5c6a63bc,
  output [7:0] L_123_a49b0d68,
  output [7:0] L_122_d75ac8bc,
  output [7:0] L_121_67e46722,
  output [7:0] L_120_34b6a3ba,
  output [7:0] L_119_83e16f30,
  output [7:0] L_118_35745232,
  output [7:0] L_117_37beb9f1,
  output [7:0] L_116_eb4bf423,
  output [7:0] L_115_378b6fa7,
  output [7:0] L_114_10d15639,
  output [7:0] L_113_4fe9915b,
  output [7:0] L_112_0ffd8e77,
  output [7:0] L_143_3745504f,
  output [7:0] L_142_6af56551,
  output [7:0] L_141_bdf5edb1,
  output [7:0] L_140_efb15ed6,
  output [7:0] L_139_8f550c1a,
  output [7:0] L_138_97eda11e,
  output [7:0] L_137_0a3513b3,
  output [7:0] L_136_546f722a,
  output [7:0] L_135_9f7935da,
  output [7:0] L_134_596005b2,
  output [7:0] L_133_f4ed92b5,
  output [7:0] L_132_b753a49c,
  output [7:0] L_131_07e5c019,
  output [7:0] L_130_edf1f25b,
  output [7:0] L_129_8f4b512c,
  output [7:0] L_128_beedcbc0,
  output [7:0] L_159_438416df,
  output [7:0] L_158_a8dd2cd8,
  output [7:0] L_157_3025f0db,
  output [7:0] L_156_579de1cf,
  output [7:0] L_155_0fb7c184,
  output [7:0] L_154_95c69e8f,
  output [7:0] L_153_cbdf0bd1,
  output [7:0] L_152_e0fd29c5,
  output [7:0] L_151_c137f5fb,
  output [7:0] L_150_7c684449,
  output [7:0] L_149_aedbc0dc,
  output [7:0] L_148_2805e3d8,
  output [7:0] L_147_486cfd5e,
  output [7:0] L_146_6e9a62c2,
  output [7:0] L_145_c25a15c7,
  output [7:0] L_144_ec1a4d9d,
  output [7:0] L_175_5fd8dca1,
  output [7:0] L_174_3938b5d2,
  output [7:0] L_173_868f5f47,
  output [7:0] L_172_84c173cb,
  output [7:0] L_171_afa03cad,
  output [7:0] L_170_a17084e7,
  output [7:0] L_169_b063b05b,
  output [7:0] L_168_3e5d9c10,
  output [7:0] L_167_583d80af,
  output [7:0] L_166_6ce6b1d2,
  output [7:0] L_165_4b39f19f,
  output [7:0] L_164_e3ad4dcd,
  output [7:0] L_163_f1205ac3,
  output [7:0] L_162_378193de,
  output [7:0] L_161_8d58ff55,
  output [7:0] L_160_30e8e70a,
  output [7:0] L_191_42c30af8,
  output [7:0] L_190_be8c7ea7,
  output [7:0] L_189_2ca3d932,
  output [7:0] L_188_0c7598d3,
  output [7:0] L_187_525802f1,
  output [7:0] L_186_0846180c,
  output [7:0] L_185_1eff2a27,
  output [7:0] L_184_3b6ae0be,
  output [7:0] L_183_d7d3aedc,
  output [7:0] L_182_06695f08,
  output [7:0] L_181_0ab10fed,
  output [7:0] L_180_02f18e6e,
  output [7:0] L_179_73e91140,
  output [7:0] L_178_32520e06,
  output [7:0] L_177_376295cf,
  output [7:0] L_176_e00acc67,
  output [7:0] L_207_d9596663,
  output [7:0] L_206_beee4402,
  output [7:0] L_205_56d0b0a5,
  output [7:0] L_204_508e99d4,
  output [7:0] L_203_bcbe93e4,
  output [7:0] L_202_82cf4e1e,
  output [7:0] L_201_bd709e47,
  output [7:0] L_200_ad9398b8,
  output [7:0] L_199_7a2c8e8c,
  output [7:0] L_198_e3703de4,
  output [7:0] L_197_a5dcd0c4,
  output [7:0] L_196_0df3d184,
  output [7:0] L_195_b21ea119,
  output [7:0] L_194_a892d091,
  output [7:0] L_193_b6a4fb0e,
  output [7:0] L_192_966b3b1b,
  output [7:0] L_223_1c13ccba,
  output [7:0] L_222_e33a5884,
  output [7:0] L_221_982e7a40,
  output [7:0] L_220_7c2af14b,
  output [7:0] L_219_5e44a710,
  output [7:0] L_218_4e23f89b,
  output [7:0] L_217_c14910f1,
  output [7:0] L_216_e5257089,
  output [7:0] L_215_2db12d0c,
  output [7:0] L_214_d5e83083,
  output [7:0] L_213_4c7eba85,
  output [7:0] L_212_8a2a5a8d,
  output [7:0] L_211_e9340d09,
  output [7:0] L_210_32305997,
  output [7:0] L_209_cc1e9a99,
  output [7:0] L_208_04a30dd2,
  output [7:0] L_239_932bc3e8,
  output [7:0] L_238_db4eae34,
  output [7:0] L_237_9847a8d5,
  output [7:0] L_236_fb6b3f93,
  output [7:0] L_235_eba3b9a0,
  output [7:0] L_234_53f3880a,
  output [7:0] L_233_38dcf616,
  output [7:0] L_232_a6252b72,
  output [7:0] L_231_a0aa18c3,
  output [7:0] L_230_079eec06,
  output [7:0] L_229_5e73c8ec,
  output [7:0] L_228_2780ed2a,
  output [7:0] L_227_5e0a05c8,
  output [7:0] L_226_50d65f3a,
  output [7:0] L_225_3caf72b0,
  output [7:0] L_224_8b1b15a3,
  output [7:0] L_255_715f482c,
  output [7:0] L_254_22eeae1a,
  output [7:0] L_253_0a063966,
  output [7:0] L_252_f85afb85,
  output [7:0] L_251_ff78a34a,
  output [7:0] L_250_f097ffeb,
  output [7:0] L_249_d979fe68,
  output [7:0] L_248_52e87327,
  output [7:0] L_247_03de5ec1,
  output [7:0] L_246_f29b66c1,
  output [7:0] L_245_61a52dc4,
  output [7:0] L_244_379bb360,
  output [7:0] L_243_9f608c5c,
  output [7:0] L_242_1ddb9925,
  output [7:0] L_241_6d61ff0f,
  output [7:0] L_240_a5ae4278
);

  wire cpu_decoder_4x16_1_l, cpu_decoder_4x16_1_m, cpu_decoder_4x16_1_out_3, cpu_decoder_4x16_1_out_4,
       cpu_decoder_4x16_1_out_5, cpu_decoder_4x16_1_out_6, cpu_decoder_4x16_1_out_7,
       cpu_decoder_4x16_1_out_8, cpu_decoder_4x16_1_out_9, cpu_decoder_4x16_1_out_10,
       cpu_decoder_4x16_1_out_11, cpu_decoder_4x16_1_out_12, cpu_decoder_4x16_1_out_13,
       cpu_decoder_4x16_1_out_14, cpu_decoder_4x16_1_out_15, cpu_decoder_4x16_1_out_16, cpu_decoder_4x16_2_l,
       cpu_decoder_4x16_2_m, cpu_decoder_4x16_2_out_3, cpu_decoder_4x16_2_out_4, cpu_decoder_4x16_2_out_5,
       cpu_decoder_4x16_2_out_6, cpu_decoder_4x16_2_out_7, cpu_decoder_4x16_2_out_8,
       cpu_decoder_4x16_2_out_9, cpu_decoder_4x16_2_out_10, cpu_decoder_4x16_2_out_11,
       cpu_decoder_4x16_2_out_12, cpu_decoder_4x16_2_out_13, cpu_decoder_4x16_2_out_14,
       cpu_decoder_4x16_2_out_15, cpu_decoder_4x16_2_out_16;
  wire [7:0] cpu_mem_8_1_out_3, cpu_reg_byte_1_o;

  CPU_MEM_8 cpu_mem_8_1 (.in_1(address), .s(sa), .out_3(cpu_mem_8_1_out_3));
  CPU_DECODER_4x16 cpu_decoder_4x16_1 (
    .in_1(cpu_mem_8_1_out_3[7:4]), .out_13(cpu_decoder_4x16_1_out_13), .out_14(cpu_decoder_4x16_1_out_14),
    .out_15(cpu_decoder_4x16_1_out_15), .out_16(cpu_decoder_4x16_1_out_16), .M(cpu_decoder_4x16_1_m),
    .L(cpu_decoder_4x16_1_l), .out_3(cpu_decoder_4x16_1_out_3), .out_4(cpu_decoder_4x16_1_out_4),
    .out_5(cpu_decoder_4x16_1_out_5), .out_6(cpu_decoder_4x16_1_out_6), .out_7(cpu_decoder_4x16_1_out_7),
    .out_8(cpu_decoder_4x16_1_out_8), .out_9(cpu_decoder_4x16_1_out_9), .out_10(cpu_decoder_4x16_1_out_10),
    .out_11(cpu_decoder_4x16_1_out_11), .out_12(cpu_decoder_4x16_1_out_12));
  assign o = e ? cpu_reg_byte_1_o : 8'bz;  // Controlled_Buffer controlled_buffer_1
  CPU_REG_BYTE cpu_reg_byte_1 (
    .h(cpu_decoder_4x16_1_l), .v(cpu_decoder_4x16_2_m), .s(s), .e(e), .RESET(reset), .i(i),
    .op(L_15_49b3f215), .o(cpu_reg_byte_1_o));
  CPU_REG_BYTE cpu_reg_byte_2 (
    .h(cpu_decoder_4x16_1_out_3), .v(cpu_decoder_4x16_2_m), .s(s), .e(e), .RESET(reset), .i(i),
    .op(L_31_244d0c43), .o(cpu_reg_byte_1_o));
  CPU_REG_BYTE cpu_reg_byte_3 (
    .h(cpu_decoder_4x16_1_l), .v(cpu_decoder_4x16_2_out_16), .s(s), .e(e), .RESET(reset), .i(i),
    .op(L_14_09a57ae2), .o(cpu_reg_byte_1_o));
  CPU_REG_BYTE cpu_reg_byte_4 (
    .h(cpu_decoder_4x16_1_out_3), .v(cpu_decoder_4x16_2_out_16), .s(s), .e(e), .RESET(reset), .i(i),
    .op(L_30_8aab3891), .o(cpu_reg_byte_1_o));
  CPU_REG_BYTE cpu_reg_byte_5 (
    .h(cpu_decoder_4x16_1_l), .v(cpu_decoder_4x16_2_out_15), .s(s), .e(e), .RESET(reset), .i(i),
    .op(L_13_b05b92d5), .o(cpu_reg_byte_1_o));
  CPU_REG_BYTE cpu_reg_byte_6 (
    .h(cpu_decoder_4x16_1_out_3), .v(cpu_decoder_4x16_2_out_15), .s(s), .e(e), .RESET(reset), .i(i),
    .op(L_29_20ac879c), .o(cpu_reg_byte_1_o));
  CPU_REG_BYTE cpu_reg_byte_7 (
    .h(cpu_decoder_4x16_1_l), .v(cpu_decoder_4x16_2_out_14), .s(s), .e(e), .RESET(reset), .i(i),
    .op(L_12_d8925d08), .o(cpu_reg_byte_1_o));
  CPU_REG_BYTE cpu_reg_byte_8 (
    .h(cpu_decoder_4x16_1_out_3), .v(cpu_decoder_4x16_2_out_14), .s(s), .e(e), .RESET(reset), .i(i),
    .op(L_28_887e6408), .o(cpu_reg_byte_1_o));
  CPU_REG_BYTE cpu_reg_byte_9 (
    .h(cpu_decoder_4x16_1_l), .v(cpu_decoder_4x16_2_out_13), .s(s), .e(e), .RESET(reset), .i(i),
    .op(L_11_d9827db8), .o(cpu_reg_byte_1_o));
  CPU_REG_BYTE cpu_reg_byte_10 (
    .h(cpu_decoder_4x16_1_out_3), .v(cpu_decoder_4x16_2_out_13), .s(s), .e(e), .RESET(reset), .i(i),
    .op(L_27_6ee616b1), .o(cpu_reg_byte_1_o));
  CPU_REG_BYTE cpu_reg_byte_11 (
    .h(cpu_decoder_4x16_1_l), .v(cpu_decoder_4x16_2_out_12), .s(s), .e(e), .RESET(reset), .i(i),
    .op(L_10_884b6e1b), .o(cpu_reg_byte_1_o));
  CPU_REG_BYTE cpu_reg_byte_12 (
    .h(cpu_decoder_4x16_1_out_3), .v(cpu_decoder_4x16_2_out_12), .s(s), .e(e), .RESET(reset), .i(i),
    .op(L_26_60793931), .o(cpu_reg_byte_1_o));
  CPU_REG_BYTE cpu_reg_byte_13 (
    .h(cpu_decoder_4x16_1_l), .v(cpu_decoder_4x16_2_out_11), .s(s), .e(e), .RESET(reset), .i(i),
    .op(L_9_e63877d4), .o(cpu_reg_byte_1_o));
  CPU_REG_BYTE cpu_reg_byte_14 (
    .h(cpu_decoder_4x16_1_out_3), .v(cpu_decoder_4x16_2_out_11), .s(s), .e(e), .RESET(reset), .i(i),
    .op(L_25_edd3a926), .o(cpu_reg_byte_1_o));
  CPU_REG_BYTE cpu_reg_byte_15 (
    .h(cpu_decoder_4x16_1_l), .v(cpu_decoder_4x16_2_out_10), .s(s), .e(e), .RESET(reset), .i(i),
    .op(L_8_0263bcbb), .o(cpu_reg_byte_1_o));
  CPU_REG_BYTE cpu_reg_byte_16 (
    .h(cpu_decoder_4x16_1_out_3), .v(cpu_decoder_4x16_2_out_10), .s(s), .e(e), .RESET(reset), .i(i),
    .op(L_24_60803382), .o(cpu_reg_byte_1_o));
  CPU_DECODER_4x16 cpu_decoder_4x16_2 (
    .in_1(cpu_mem_8_1_out_3[3:0]), .out_13(cpu_decoder_4x16_2_out_13), .out_14(cpu_decoder_4x16_2_out_14),
    .out_15(cpu_decoder_4x16_2_out_15), .out_16(cpu_decoder_4x16_2_out_16), .M(cpu_decoder_4x16_2_m),
    .L(cpu_decoder_4x16_2_l), .out_3(cpu_decoder_4x16_2_out_3), .out_4(cpu_decoder_4x16_2_out_4),
    .out_5(cpu_decoder_4x16_2_out_5), .out_6(cpu_decoder_4x16_2_out_6), .out_7(cpu_decoder_4x16_2_out_7),
    .out_8(cpu_decoder_4x16_2_out_8), .out_9(cpu_decoder_4x16_2_out_9), .out_10(cpu_decoder_4x16_2_out_10),
    .out_11(cpu_decoder_4x16_2_out_11), .out_12(cpu_decoder_4x16_2_out_12));
  CPU_REG_BYTE cpu_reg_byte_17 (
    .h(cpu_decoder_4x16_1_l), .v(cpu_decoder_4x16_2_out_9), .s(s), .e(e), .RESET(reset), .i(i),
    .op(L_7_21e06148), .o(cpu_reg_byte_1_o));
  CPU_REG_BYTE cpu_reg_byte_18 (
    .h(cpu_decoder_4x16_1_out_3), .v(cpu_decoder_4x16_2_out_9), .s(s), .e(e), .RESET(reset), .i(i),
    .op(L_23_5bebf840), .o(cpu_reg_byte_1_o));
  CPU_REG_BYTE cpu_reg_byte_19 (
    .h(cpu_decoder_4x16_1_l), .v(cpu_decoder_4x16_2_out_8), .s(s), .e(e), .RESET(reset), .i(i),
    .op(L_6_35fe27e4), .o(cpu_reg_byte_1_o));
  CPU_REG_BYTE cpu_reg_byte_20 (
    .h(cpu_decoder_4x16_1_out_3), .v(cpu_decoder_4x16_2_out_8), .s(s), .e(e), .RESET(reset), .i(i),
    .op(L_22_3fa04d94), .o(cpu_reg_byte_1_o));
  CPU_REG_BYTE cpu_reg_byte_21 (
    .h(cpu_decoder_4x16_1_l), .v(cpu_decoder_4x16_2_out_7), .s(s), .e(e), .RESET(reset), .i(i),
    .op(L_5_5a09c7b9), .o(cpu_reg_byte_1_o));
  CPU_REG_BYTE cpu_reg_byte_22 (
    .h(cpu_decoder_4x16_1_out_3), .v(cpu_decoder_4x16_2_out_7), .s(s), .e(e), .RESET(reset), .i(i),
    .op(L_21_2793d292), .o(cpu_reg_byte_1_o));
  CPU_REG_BYTE cpu_reg_byte_23 (
    .h(cpu_decoder_4x16_1_l), .v(cpu_decoder_4x16_2_out_6), .s(s), .e(e), .RESET(reset), .i(i),
    .op(L_4_df9eb970), .o(cpu_reg_byte_1_o));
  CPU_REG_BYTE cpu_reg_byte_24 (
    .h(cpu_decoder_4x16_1_out_3), .v(cpu_decoder_4x16_2_out_6), .s(s), .e(e), .RESET(reset), .i(i),
    .op(L_20_b0f18e1f), .o(cpu_reg_byte_1_o));
  CPU_REG_BYTE cpu_reg_byte_25 (
    .h(cpu_decoder_4x16_1_l), .v(cpu_decoder_4x16_2_out_5), .s(s), .e(e), .RESET(reset), .i(i), .op(out_20),
    .o(cpu_reg_byte_1_o));
  CPU_REG_BYTE cpu_reg_byte_26 (
    .h(cpu_decoder_4x16_1_out_3), .v(cpu_decoder_4x16_2_out_5), .s(s), .e(e), .RESET(reset), .i(i),
    .op(L_19_df0ab950), .o(cpu_reg_byte_1_o));
  CPU_REG_BYTE cpu_reg_byte_27 (
    .h(cpu_decoder_4x16_1_l), .v(cpu_decoder_4x16_2_out_4), .s(s), .e(e), .RESET(reset), .i(i),
    .op(L_2_021c411d), .o(cpu_reg_byte_1_o));
  CPU_REG_BYTE cpu_reg_byte_28 (
    .h(cpu_decoder_4x16_1_out_3), .v(cpu_decoder_4x16_2_out_4), .s(s), .e(e), .RESET(reset), .i(i),
    .op(L_18_77c23569), .o(cpu_reg_byte_1_o));
  CPU_REG_BYTE cpu_reg_byte_29 (
    .h(cpu_decoder_4x16_1_l), .v(cpu_decoder_4x16_2_out_3), .s(s), .e(e), .RESET(reset), .i(i),
    .op(L_1_a0dbb3e4), .o(cpu_reg_byte_1_o));
  CPU_REG_BYTE cpu_reg_byte_30 (
    .h(cpu_decoder_4x16_1_out_3), .v(cpu_decoder_4x16_2_out_3), .s(s), .e(e), .RESET(reset), .i(i),
    .op(L_17_a6f2001c), .o(cpu_reg_byte_1_o));
  CPU_REG_BYTE cpu_reg_byte_31 (
    .h(cpu_decoder_4x16_1_l), .v(cpu_decoder_4x16_2_l), .s(s), .e(e), .RESET(reset), .i(i),
    .op(L_0_0718cde6), .o(cpu_reg_byte_1_o));
  CPU_REG_BYTE cpu_reg_byte_32 (
    .h(cpu_decoder_4x16_1_out_3), .v(cpu_decoder_4x16_2_l), .s(s), .e(e), .RESET(reset), .i(i),
    .op(L_16_4a4ef9fa), .o(cpu_reg_byte_1_o));

  // Notes on the sheet:
  //   address: pull=down
  //   L_7_21e06148: pull=up
  //   L_6_35fe27e4: pull=up
  //   L_4_df9eb970: pull=up
  //   L_2_021c411d: pull=up
  //   L_0_0718cde6: pull=down
  //   o: pull=down
  //   reset: pull=down
  //   i: pull=down
  //   sa: pull=down
endmodule

module CPU_NOT (
  input  [7:0] i,
  output [7:0] out_2
);

  not not_1 (out_2[0], i[0]);
  not not_2 (out_2[1], i[1]);
  not not_3 (out_2[2], i[2]);
  not not_4 (out_2[3], i[3]);
  not not_5 (out_2[4], i[4]);
  not not_6 (out_2[5], i[5]);
  not not_7 (out_2[6], i[6]);
  not not_8 (out_2[7], i[7]);
endmodule

module CPU_AND (
  input  [7:0] a,
  input  [7:0] b,
  output [7:0] o
);

  and and_1 (o[0], a[0], b[0]);
  and and_2 (o[1], a[1], b[1]);
  and and_3 (o[2], a[2], b[2]);
  and and_4 (o[3], a[3], b[3]);
  and and_5 (o[4], a[4], b[4]);
  and and_6 (o[5], a[5], b[5]);
  and and_7 (o[6], a[6], b[6]);
  and and_8 (o[7], a[7], b[7]);
endmodule

module CPU_OR (
  input  [7:0] a,
  input  [7:0] b,
  output [7:0] L_0_0718cde6
);

  or or_1 (L_0_0718cde6[0], a[0], b[0]);
  or or_2 (L_0_0718cde6[1], a[1], b[1]);
  or or_3 (L_0_0718cde6[2], a[2], b[2]);
  or or_4 (L_0_0718cde6[3], a[3], b[3]);
  or or_5 (L_0_0718cde6[4], a[4], b[4]);
  or or_6 (L_0_0718cde6[5], a[5], b[5]);
  or or_7 (L_0_0718cde6[6], a[6], b[6]);
  or or_8 (L_0_0718cde6[7], a[7], b[7]);
endmodule

module CPU_XOR_1 (
  input  a,
  input  b,
  output o
);

  wire nand_1_out, nand_2_out, not_1_out, not_2_out;

  not not_1 (not_1_out, a);
  not not_2 (not_2_out, b);
  nand nand_1 (nand_1_out, not_1_out, b);
  nand nand_2 (nand_2_out, a, not_2_out);
  nand nand_3 (o, nand_1_out, nand_2_out);
endmodule

module CPU_SHR (
  input  [7:0] i,
  input  shift_in_93523f6f,
  output shift_out_58d098f0,
  output [7:0] o
);

  wire [7:1] cpu_register_8_1_l_0_0718cde6;

  CPU_REGISTER_8 cpu_register_8_1 (
    .i(i), .s(1'b1), .e(1'b1), .L_0_0718cde6({cpu_register_8_1_l_0_0718cde6, shift_out_58d098f0}));  // open: REG
  CPU_REGISTER_8 cpu_register_8_2 (
    .i({shift_in_93523f6f, cpu_register_8_1_l_0_0718cde6}), .s(1'b1), .e(1'b1), .L_0_0718cde6(o));  // open: REG
endmodule

module CPU_SHL (
  input  shift_in_93523f6f,
  input  [7:0] i,
  output [7:0] o,
  output shift_out_58d098f0
);

  wire [6:0] cpu_register_8_1_l_0_0718cde6;

  CPU_REGISTER_8 cpu_register_8_1 (
    .i(i), .s(1'b1), .e(1'b1), .L_0_0718cde6({shift_out_58d098f0, cpu_register_8_1_l_0_0718cde6}));  // open: REG
  CPU_REGISTER_8 cpu_register_8_2 (
    .i({cpu_register_8_1_l_0_0718cde6, shift_in_93523f6f}), .s(1'b1), .e(1'b1), .L_0_0718cde6(o));  // open: REG
endmodule

module CPU_ADDER (
  input  a,
  input  b,
  input  carry_in_a6733c17,
  output sum,
  output carry_out_b6478916
);

  wire and_1_out, and_2_out, cpu_xor_1_1_o;

  CPU_XOR_1 cpu_xor_1_1 (.a(a), .b(b), .o(cpu_xor_1_1_o));
  and and_1 (and_1_out, carry_in_a6733c17, cpu_xor_1_1_o);
  and and_2 (and_2_out, a, b);
  CPU_XOR_1 cpu_xor_1_2 (.a(cpu_xor_1_1_o), .b(carry_in_a6733c17), .o(sum));
  or or_1 (carry_out_b6478916, and_1_out, and_2_out);
endmodule

module CPU_ADDER_8 (
  input  [7:0] a,
  input  [7:0] b,
  input  carry_in_a6733c17,
  output carry_out_b6478916,
  output [7:0] out_5
);

  wire cpu_adder_2_carry_out_b6478916, cpu_adder_3_carry_out_b6478916, cpu_adder_4_carry_out_b6478916,
       cpu_adder_5_carry_out_b6478916, cpu_adder_6_carry_out_b6478916, cpu_adder_7_carry_out_b6478916,
       cpu_adder_8_carry_out_b6478916;

  CPU_ADDER cpu_adder_1 (
    .carry_in_a6733c17(cpu_adder_2_carry_out_b6478916), .a(a[7]), .b(b[7]), .sum(out_5[7]),
    .carry_out_b6478916(carry_out_b6478916));
  CPU_ADDER cpu_adder_2 (
    .carry_in_a6733c17(cpu_adder_3_carry_out_b6478916), .a(a[6]), .b(b[6]), .sum(out_5[6]),
    .carry_out_b6478916(cpu_adder_2_carry_out_b6478916));
  CPU_ADDER cpu_adder_3 (
    .carry_in_a6733c17(cpu_adder_4_carry_out_b6478916), .a(a[5]), .b(b[5]), .sum(out_5[5]),
    .carry_out_b6478916(cpu_adder_3_carry_out_b6478916));
  CPU_ADDER cpu_adder_4 (
    .carry_in_a6733c17(cpu_adder_5_carry_out_b6478916), .a(a[4]), .b(b[4]), .sum(out_5[4]),
    .carry_out_b6478916(cpu_adder_4_carry_out_b6478916));
  CPU_ADDER cpu_adder_5 (
    .carry_in_a6733c17(cpu_adder_6_carry_out_b6478916), .a(a[3]), .b(b[3]), .sum(out_5[3]),
    .carry_out_b6478916(cpu_adder_5_carry_out_b6478916));
  CPU_ADDER cpu_adder_6 (
    .carry_in_a6733c17(cpu_adder_7_carry_out_b6478916), .a(a[2]), .b(b[2]), .sum(out_5[2]),
    .carry_out_b6478916(cpu_adder_6_carry_out_b6478916));
  CPU_ADDER cpu_adder_7 (
    .carry_in_a6733c17(cpu_adder_8_carry_out_b6478916), .a(a[1]), .b(b[1]), .sum(out_5[1]),
    .carry_out_b6478916(cpu_adder_7_carry_out_b6478916));
  CPU_ADDER cpu_adder_8 (
    .carry_in_a6733c17(carry_in_a6733c17), .a(a[0]), .b(b[0]), .sum(out_5[0]),
    .carry_out_b6478916(cpu_adder_8_carry_out_b6478916));
endmodule

module CPU_XOR_LE_1 (
  input  above_equal_99b73a17,
  input  a_larger_86161fbd,
  input  a,
  input  b,
  output c,
  output equal,
  output a_large
);

  wire and_2_out, not_1_out;

  CPU_XOR_1 cpu_xor_1_1 (.a(a), .b(b), .o(c));
  not not_1 (not_1_out, c);
  and and_1 (equal, not_1_out, above_equal_99b73a17);
  and and_2 (and_2_out, above_equal_99b73a17, a, c);
  or or_1 (a_large, and_2_out, a_larger_86161fbd);
endmodule

module CPU_XOR_LE_8 (
  input  [7:0] a,
  input  [7:0] b,
  output [7:0] out_3,
  output larger,
  output equal
);

  wire cpu_xor_le_1_1_a_large, cpu_xor_le_1_1_equal, cpu_xor_le_1_2_a_large, cpu_xor_le_1_2_equal,
       cpu_xor_le_1_3_a_large, cpu_xor_le_1_3_equal, cpu_xor_le_1_4_a_large, cpu_xor_le_1_4_equal,
       cpu_xor_le_1_5_a_large, cpu_xor_le_1_5_equal, cpu_xor_le_1_6_a_large, cpu_xor_le_1_6_equal,
       cpu_xor_le_1_7_a_large, cpu_xor_le_1_7_equal;

  CPU_XOR_LE_1 cpu_xor_le_1_1 (
    .a(a[7]), .b(b[7]), .above_equal_99b73a17(1'b1), .a_larger_86161fbd(1'b0), .equal(cpu_xor_le_1_1_equal),
    .a_large(cpu_xor_le_1_1_a_large), .c(out_3[7]));
  CPU_XOR_LE_1 cpu_xor_le_1_2 (
    .a(a[6]), .b(b[6]), .above_equal_99b73a17(cpu_xor_le_1_1_equal),
    .a_larger_86161fbd(cpu_xor_le_1_1_a_large), .equal(cpu_xor_le_1_2_equal),
    .a_large(cpu_xor_le_1_2_a_large), .c(out_3[6]));
  CPU_XOR_LE_1 cpu_xor_le_1_3 (
    .a(a[5]), .b(b[5]), .above_equal_99b73a17(cpu_xor_le_1_2_equal),
    .a_larger_86161fbd(cpu_xor_le_1_2_a_large), .equal(cpu_xor_le_1_3_equal),
    .a_large(cpu_xor_le_1_3_a_large), .c(out_3[5]));
  CPU_XOR_LE_1 cpu_xor_le_1_4 (
    .a(a[4]), .b(b[4]), .above_equal_99b73a17(cpu_xor_le_1_3_equal),
    .a_larger_86161fbd(cpu_xor_le_1_3_a_large), .equal(cpu_xor_le_1_4_equal),
    .a_large(cpu_xor_le_1_4_a_large), .c(out_3[4]));
  CPU_XOR_LE_1 cpu_xor_le_1_5 (
    .a(a[3]), .b(b[3]), .above_equal_99b73a17(cpu_xor_le_1_4_equal),
    .a_larger_86161fbd(cpu_xor_le_1_4_a_large), .equal(cpu_xor_le_1_5_equal),
    .a_large(cpu_xor_le_1_5_a_large), .c(out_3[3]));
  CPU_XOR_LE_1 cpu_xor_le_1_6 (
    .a(a[2]), .b(b[2]), .above_equal_99b73a17(cpu_xor_le_1_5_equal),
    .a_larger_86161fbd(cpu_xor_le_1_5_a_large), .equal(cpu_xor_le_1_6_equal),
    .a_large(cpu_xor_le_1_6_a_large), .c(out_3[2]));
  CPU_XOR_LE_1 cpu_xor_le_1_7 (
    .a(a[1]), .b(b[1]), .above_equal_99b73a17(cpu_xor_le_1_6_equal),
    .a_larger_86161fbd(cpu_xor_le_1_6_a_large), .equal(cpu_xor_le_1_7_equal),
    .a_large(cpu_xor_le_1_7_a_large), .c(out_3[1]));
  CPU_XOR_LE_1 cpu_xor_le_1_8 (
    .a(a[0]), .b(b[0]), .above_equal_99b73a17(cpu_xor_le_1_7_equal),
    .a_larger_86161fbd(cpu_xor_le_1_7_a_large), .equal(equal), .a_large(larger), .c(out_3[0]));
endmodule

module CPU_Z (
  input  [7:0] i,
  output o
);

  wire or_1_out;

  or or_1 (or_1_out, i[0], i[1], i[2], i[3], i[4], i[5], i[6], i[7]);
  not not_1 (o, or_1_out);
endmodule

module CPU_DECODER_3x8 (
  input  c,
  input  b,
  input  a,
  output [7:0] o
);

  wire not_1_out, not_2_out, not_3_out;

  not not_1 (not_1_out, a);
  not not_2 (not_2_out, b);
  not not_3 (not_3_out, c);
  and and_1 (o[0], not_3_out, not_2_out, not_1_out);
  and and_2 (o[1], not_3_out, not_2_out, a);
  and and_3 (o[2], not_3_out, b, not_1_out);
  and and_4 (o[3], not_3_out, b, a);
  and and_5 (o[4], c, not_2_out, not_1_out);
  and and_6 (o[5], c, not_2_out, a);
  and and_7 (o[6], c, b, not_1_out);
  and and_8 (o[7], c, b, a);

  // Notes on the sheet:
  //   a: pull=down
  //   c: pull=down
  //   b: pull=down
  //   o: pull=down
  //   msb
  //   lsb
endmodule

module CPU_E (
  input  [7:0] in_1,
  input  in_2,
  output [7:0] out_3
);

  wire and_1_out, and_2_out, and_3_out, and_4_out, and_5_out, and_6_out, and_7_out, and_8_out;

  and and_1 (and_1_out, in_1[0], in_2);
  assign out_3[0] = in_2 ? and_1_out : 1'bz;  // Controlled_Buffer controlled_buffer_1
  and and_2 (and_2_out, in_1[1], in_2);
  assign out_3[1] = in_2 ? and_2_out : 1'bz;  // Controlled_Buffer controlled_buffer_2
  and and_3 (and_3_out, in_1[2], in_2);
  assign out_3[2] = in_2 ? and_3_out : 1'bz;  // Controlled_Buffer controlled_buffer_3
  and and_4 (and_4_out, in_1[3], in_2);
  assign out_3[3] = in_2 ? and_4_out : 1'bz;  // Controlled_Buffer controlled_buffer_4
  and and_5 (and_5_out, in_1[4], in_2);
  assign out_3[4] = in_2 ? and_5_out : 1'bz;  // Controlled_Buffer controlled_buffer_5
  and and_6 (and_6_out, in_1[5], in_2);
  assign out_3[5] = in_2 ? and_6_out : 1'bz;  // Controlled_Buffer controlled_buffer_6
  and and_7 (and_7_out, in_1[6], in_2);
  assign out_3[6] = in_2 ? and_7_out : 1'bz;  // Controlled_Buffer controlled_buffer_7
  and and_8 (and_8_out, in_1[7], in_2);
  assign out_3[7] = in_2 ? and_8_out : 1'bz;  // Controlled_Buffer controlled_buffer_8
endmodule

module CPU_ALU (
  input  [7:0] in_1,
  input  [7:0] in_2,
  input  carry_in_a6733c17,
  input  a,
  input  b,
  input  c,
  output a_larger_86161fbd,
  output equal,
  output zero,
  output [7:0] out_10,
  output carry_out_b6478916
);

  wire and_1_out, and_2_out, and_3_out, cpu_adder_8_1_carry_out_b6478916, cpu_shl_1_shift_out_58d098f0,
       cpu_shr_1_shift_out_58d098f0;
  wire [7:0] cpu_adder_8_1_out_5, cpu_and_1_o, cpu_decoder_3x8_1_o, cpu_not_1_out_2, cpu_or_1_l_0_0718cde6,
       cpu_shl_1_o, cpu_shr_1_o, cpu_xor_le_8_1_out_3;

  CPU_XOR_LE_8 cpu_xor_le_8_1 (
    .a(in_1), .b(in_2), .larger(a_larger_86161fbd), .equal(equal), .out_3(cpu_xor_le_8_1_out_3));
  CPU_AND cpu_and_1 (.b(in_2), .a(in_1), .o(cpu_and_1_o));
  CPU_NOT cpu_not_1 (.i(in_1), .out_2(cpu_not_1_out_2));
  CPU_SHL cpu_shl_1 (
    .shift_in_93523f6f(carry_in_a6733c17), .i(in_1), .shift_out_58d098f0(cpu_shl_1_shift_out_58d098f0),
    .o(cpu_shl_1_o));
  CPU_SHR cpu_shr_1 (
    .shift_in_93523f6f(carry_in_a6733c17), .i(in_1), .shift_out_58d098f0(cpu_shr_1_shift_out_58d098f0),
    .o(cpu_shr_1_o));
  CPU_ADDER_8 cpu_adder_8_1 (
    .b(in_2), .a(in_1), .carry_in_a6733c17(carry_in_a6733c17),
    .carry_out_b6478916(cpu_adder_8_1_carry_out_b6478916), .out_5(cpu_adder_8_1_out_5));
  CPU_OR cpu_or_1 (.a(in_1), .b(in_2), .L_0_0718cde6(cpu_or_1_l_0_0718cde6));
  CPU_DECODER_3x8 cpu_decoder_3x8_1 (.a(a), .c(c), .b(b), .o(cpu_decoder_3x8_1_o));
  CPU_E cpu_e_1 (.in_1(cpu_xor_le_8_1_out_3), .in_2(cpu_decoder_3x8_1_o[6]), .out_3(out_10));
  CPU_E cpu_e_2 (.in_1(cpu_or_1_l_0_0718cde6), .in_2(cpu_decoder_3x8_1_o[5]), .out_3(out_10));
  CPU_E cpu_e_3 (.in_1(cpu_and_1_o), .in_2(cpu_decoder_3x8_1_o[4]), .out_3(out_10));
  CPU_E cpu_e_4 (.in_1(cpu_not_1_out_2), .in_2(cpu_decoder_3x8_1_o[3]), .out_3(out_10));
  CPU_E cpu_e_5 (.in_1(cpu_shl_1_o), .in_2(cpu_decoder_3x8_1_o[2]), .out_3(out_10));
  CPU_E cpu_e_6 (.in_1(cpu_shr_1_o), .in_2(cpu_decoder_3x8_1_o[1]), .out_3(out_10));
  CPU_E cpu_e_7 (.in_1(cpu_adder_8_1_out_5), .in_2(cpu_decoder_3x8_1_o[0]), .out_3(out_10));
  and and_1 (and_1_out, cpu_shl_1_shift_out_58d098f0, cpu_decoder_3x8_1_o[2]);
  assign carry_out_b6478916 = cpu_decoder_3x8_1_o[2] ? and_1_out : 1'bz;  // Controlled_Buffer controlled_buffer_1
  and and_2 (and_2_out, cpu_shr_1_shift_out_58d098f0, cpu_decoder_3x8_1_o[1]);
  assign carry_out_b6478916 = cpu_decoder_3x8_1_o[1] ? and_2_out : 1'bz;  // Controlled_Buffer controlled_buffer_2
  and and_3 (and_3_out, cpu_adder_8_1_carry_out_b6478916, cpu_decoder_3x8_1_o[0]);
  assign carry_out_b6478916 = cpu_decoder_3x8_1_o[0] ? and_3_out : 1'bz;  // Controlled_Buffer controlled_buffer_3
  CPU_Z cpu_z_1 (.i(out_10), .o(zero));

  // Notes on the sheet:
  //   out_10: pull=down
  //   carry_out_b6478916: pull=down
  //   zero: pull=down
  //   a: pull=down
  //   b: pull=down
  //   c: pull=down
  //   in_1: pull=down
  //   in_2: pull=down
  //   carry_in_a6733c17: pull=down
  //   a_larger_86161fbd: pull=down
  //   equal: pull=down
endmodule

module CPU_BUS_1 (
  input  [7:0] i,
  input  bus_1_9bcc1f1f,
  output [7:0] o
);

  wire not_1_out;

  and and_1 (o[7], i[7], not_1_out);
  and and_2 (o[6], i[6], not_1_out);
  and and_3 (o[5], i[5], not_1_out);
  and and_4 (o[4], i[4], not_1_out);
  and and_5 (o[3], i[3], not_1_out);
  and and_6 (o[2], i[2], not_1_out);
  and and_7 (o[1], i[1], not_1_out);
  not not_1 (not_1_out, bus_1_9bcc1f1f);
  or or_1 (o[0], i[0], bus_1_9bcc1f1f);

  // Notes on the sheet:
  //   bus_1_9bcc1f1f: pull=down
  //   i: pull=down
  //   o: pull=down
endmodule

module CPU_ACCUMULATOR (
  input  [7:0] i,
  input  s,
  input  e,
  output [7:0] ACC,
  output [7:0] o
);

  CPU_REGISTER_8 cpu_register_8_1 (.i(i), .s(s), .e(e), .REG(ACC), .L_0_0718cde6(o));

  // Notes on the sheet:
  //   i: pull=down
  //   s: pull=down
  //   e: pull=down
  //   o: pull=down
endmodule

module CPU_R (
  input  [7:0] i,
  input  s,
  input  e,
  output [7:0] \reg ,
  output [7:0] o
);

  CPU_REGISTER_8 cpu_register_8_1 (.i(i), .s(s), .e(e), .REG(\reg ), .L_0_0718cde6(o));

  // Notes on the sheet:
  //   i: pull=down
  //   s: pull=down
  //   e: pull=down
  //   o: pull=down
endmodule

module CPU_TMP (
  input  [7:0] i,
  input  s,
  output [7:0] o
);

  wire [7:0] controlled_buffer_1_out;

  assign controlled_buffer_1_out = s ? i : 8'bz;  // Controlled_Buffer controlled_buffer_1
  CPU_MEM_8 cpu_mem_8_1 (.in_1(controlled_buffer_1_out), .s(s), .out_3(o));

  // Notes on the sheet:
  //   i: pull=down
  //   s: pull=down
  //   o: pull=down
endmodule

module CPU_STEPPER (
  input  reset,
  input  clk,
  output step_1_4896c425,
  output step_2_d28dd23a,
  output step_3_5d5bb038,
  output step_4_6f30b4e7,
  output step_5_fb56fd61,
  output step_6_3a46c3ff,
  output step_7_7823715d
);

  wire cpu_mem_1_1_out_3, cpu_mem_1_2_out_3, cpu_mem_1_3_out_3, cpu_mem_1_4_out_3, cpu_mem_1_5_out_3,
       cpu_mem_1_6_out_3, cpu_mem_1_7_out_3, cpu_mem_1_8_out_3, cpu_mem_1_9_out_3, cpu_mem_1_10_out_3,
       cpu_mem_1_11_out_3, not_1_out, not_2_out, not_3_out, not_4_out, not_5_out, not_6_out, not_7_out,
       not_8_out, or_1_out, or_2_out;

  not not_1 (not_1_out, clk);
  not not_2 (not_2_out, reset);
  or or_1 (or_1_out, reset, clk);
  or or_2 (or_2_out, reset, not_1_out);
  or or_3 (step_1_4896c425, reset, not_3_out);
  CPU_MEM_1 cpu_mem_1_1 (.in_2(or_1_out), .in_1(not_2_out), .out_3(cpu_mem_1_1_out_3));
  not not_3 (not_3_out, cpu_mem_1_2_out_3);
  CPU_MEM_1 cpu_mem_1_2 (.in_2(or_2_out), .in_1(cpu_mem_1_1_out_3), .out_3(cpu_mem_1_2_out_3));
  and and_1 (step_2_d28dd23a, cpu_mem_1_2_out_3, not_4_out);
  not not_4 (not_4_out, cpu_mem_1_4_out_3);
  CPU_MEM_1 cpu_mem_1_3 (.in_2(or_1_out), .in_1(cpu_mem_1_2_out_3), .out_3(cpu_mem_1_3_out_3));
  CPU_MEM_1 cpu_mem_1_4 (.in_2(or_2_out), .in_1(cpu_mem_1_3_out_3), .out_3(cpu_mem_1_4_out_3));
  and and_2 (step_3_5d5bb038, cpu_mem_1_4_out_3, not_5_out);
  CPU_MEM_1 cpu_mem_1_5 (.in_2(or_1_out), .in_1(cpu_mem_1_4_out_3), .out_3(cpu_mem_1_5_out_3));
  not not_5 (not_5_out, cpu_mem_1_6_out_3);
  CPU_MEM_1 cpu_mem_1_6 (.in_2(or_2_out), .in_1(cpu_mem_1_5_out_3), .out_3(cpu_mem_1_6_out_3));
  and and_3 (step_4_6f30b4e7, cpu_mem_1_6_out_3, not_6_out);
  not not_6 (not_6_out, cpu_mem_1_8_out_3);
  CPU_MEM_1 cpu_mem_1_7 (.in_2(or_1_out), .in_1(cpu_mem_1_6_out_3), .out_3(cpu_mem_1_7_out_3));
  and and_4 (step_5_fb56fd61, cpu_mem_1_8_out_3, not_7_out);
  CPU_MEM_1 cpu_mem_1_8 (.in_2(or_2_out), .in_1(cpu_mem_1_7_out_3), .out_3(cpu_mem_1_8_out_3));
  CPU_MEM_1 cpu_mem_1_9 (.in_2(or_1_out), .in_1(cpu_mem_1_8_out_3), .out_3(cpu_mem_1_9_out_3));
  not not_7 (not_7_out, cpu_mem_1_10_out_3);
  CPU_MEM_1 cpu_mem_1_10 (.in_2(or_2_out), .in_1(cpu_mem_1_9_out_3), .out_3(cpu_mem_1_10_out_3));
  and and_5 (step_6_3a46c3ff, cpu_mem_1_10_out_3, not_8_out);
  CPU_MEM_1 cpu_mem_1_11 (.in_2(or_1_out), .in_1(cpu_mem_1_10_out_3), .out_3(cpu_mem_1_11_out_3));
  not not_8 (not_8_out, step_7_7823715d);
  CPU_MEM_1 cpu_mem_1_12 (.in_2(or_2_out), .in_1(cpu_mem_1_11_out_3), .out_3(step_7_7823715d));

  // Notes on the sheet:
  //   reset: pull=down
endmodule

module CPU (
  input  clock,
  input  LOAD,
  input  MARS,
  input  [7:0] RAM_INPUT_ad5b00f9,
  input  RESET,
  output [7:0] R0,
  output [7:0] R1,
  output [7:0] R2,
  output [7:0] R3,
  output clkl,
  output clke,
  output clks,
  output END,
  output S,
  output E,
  output IO,
  output DA,
  output [7:0] out_18,
  output [7:0] out_19,
  output [7:0] out_20,
  output [7:0] BUS_OUTPUT_8a49af3e
);

  wire and_1_out, and_2_out, and_3_out, C, cpu_alu_1_a_larger_86161fbd, cpu_alu_1_carry_out_b6478916,
       cpu_alu_1_equal, cpu_alu_1_zero, cpu_carry_temp_1_o, cpu_control_section_4b4a8754_1_acc_e,
       cpu_control_section_4b4a8754_1_acc_s, cpu_control_section_4b4a8754_1_alu_0,
       cpu_control_section_4b4a8754_1_alu_1, cpu_control_section_4b4a8754_1_alu_2,
       cpu_control_section_4b4a8754_1_bus_1_0aec77e3, cpu_control_section_4b4a8754_1_flags_s,
       cpu_control_section_4b4a8754_1_iar_e, cpu_control_section_4b4a8754_1_iar_s,
       cpu_control_section_4b4a8754_1_ir_s, cpu_control_section_4b4a8754_1_mar_s,
       cpu_control_section_4b4a8754_1_r0_e, cpu_control_section_4b4a8754_1_r0_s,
       cpu_control_section_4b4a8754_1_r1_e, cpu_control_section_4b4a8754_1_r1_s,
       cpu_control_section_4b4a8754_1_r2_e, cpu_control_section_4b4a8754_1_r2_s,
       cpu_control_section_4b4a8754_1_r3_e, cpu_control_section_4b4a8754_1_r3_s,
       cpu_control_section_4b4a8754_1_ram_e, cpu_control_section_4b4a8754_1_ram_s, cpu_flags_1_out_6,
       cpu_flags_1_out_7, cpu_flags_1_out_8, cpu_flags_1_out_9, not_1_out, S_t;
  wire [7:0] cpu_alu_1_out_10, cpu_bus_1_1_o, cpu_ram_256_1_l_56_a274d823, cpu_tmp_1_o,
       load_256_count_1_count, multiplexer_1_out;

  CPU_ACCUMULATOR cpu_accumulator_1 (
    .i(cpu_alu_1_out_10), .s(cpu_control_section_4b4a8754_1_acc_s), .e(cpu_control_section_4b4a8754_1_acc_e),
    .ACC(out_20), .o(BUS_OUTPUT_8a49af3e));
  CPU_TMP cpu_tmp_1 (.i(BUS_OUTPUT_8a49af3e), .s(S_t), .o(cpu_tmp_1_o));
  CPU_BUS_1 cpu_bus_1_1 (
    .bus_1_9bcc1f1f(cpu_control_section_4b4a8754_1_bus_1_0aec77e3), .i(cpu_tmp_1_o), .o(cpu_bus_1_1_o));
  CPU_ALU cpu_alu_1 (
    .a(cpu_control_section_4b4a8754_1_alu_0), .b(cpu_control_section_4b4a8754_1_alu_1),
    .c(cpu_control_section_4b4a8754_1_alu_2), .in_1(BUS_OUTPUT_8a49af3e), .in_2(cpu_bus_1_1_o),
    .carry_in_a6733c17(and_2_out), .out_10(cpu_alu_1_out_10),
    .carry_out_b6478916(cpu_alu_1_carry_out_b6478916), .zero(cpu_alu_1_zero),
    .a_larger_86161fbd(cpu_alu_1_a_larger_86161fbd), .equal(cpu_alu_1_equal));
  not not_1 (not_1_out, END);
  and and_1 (and_1_out, clock, not_1_out);
  and and_2 (and_2_out, cpu_carry_temp_1_o, C);
  and and_3 (and_3_out, LOAD, clkl);
  CPU_CLK cpu_clk_1 (.clkin(and_1_out), .clk(clkl), .clks(clks), .clke(clke));
  CPU_CARRY_TEMP cpu_carry_temp_1 (.c(cpu_flags_1_out_6), .s(S_t), .o(cpu_carry_temp_1_o));
  CPU_FLAGS cpu_flags_1 (
    .C(cpu_alu_1_carry_out_b6478916), .A(cpu_alu_1_a_larger_86161fbd), .E(cpu_alu_1_equal),
    .Z(cpu_alu_1_zero), .s(cpu_control_section_4b4a8754_1_flags_s), .out_6(cpu_flags_1_out_6),
    .out_7(cpu_flags_1_out_7), .out_8(cpu_flags_1_out_8), .out_9(cpu_flags_1_out_9));
  LOAD_256_COUNT load_256_count_1 (.clk(and_3_out), .count(load_256_count_1_count));  // open: carry
  assign BUS_OUTPUT_8a49af3e = LOAD ? load_256_count_1_count : 8'bz;  // Controlled_Buffer controlled_buffer_1
  CPU_CONTROL_SECTION_4b4a8754 cpu_control_section_4b4a8754_1 (
    .MARS(MARS), .RESET(RESET), .clke(clke), .clks(clks), .clk(clkl), .C(cpu_flags_1_out_6),
    .A(cpu_flags_1_out_7), .E(cpu_flags_1_out_8), .Z(cpu_flags_1_out_9), .LOAD(LOAD),
    .IR_IN_c6fa6e43(out_18), .RAM_E(cpu_control_section_4b4a8754_1_ram_e),
    .R0_E(cpu_control_section_4b4a8754_1_r0_e), .R1_E(cpu_control_section_4b4a8754_1_r1_e),
    .R2_E(cpu_control_section_4b4a8754_1_r2_e), .R3_E(cpu_control_section_4b4a8754_1_r3_e),
    .IO_CLKS_S_d3c82ef0(S), .END(END), .IO(IO), .DA(DA), .R0_S(cpu_control_section_4b4a8754_1_r0_s),
    .R1_S(cpu_control_section_4b4a8754_1_r1_s), .R2_S(cpu_control_section_4b4a8754_1_r2_s),
    .R3_S(cpu_control_section_4b4a8754_1_r3_s), .IR_S(cpu_control_section_4b4a8754_1_ir_s),
    .IAR_S(cpu_control_section_4b4a8754_1_iar_s), .ACC_S(cpu_control_section_4b4a8754_1_acc_s), .TMP_S(S_t),
    .FLAGS_S(cpu_control_section_4b4a8754_1_flags_s), .MAR_S(cpu_control_section_4b4a8754_1_mar_s),
    .RAM_S(cpu_control_section_4b4a8754_1_ram_s), .ACC_E(cpu_control_section_4b4a8754_1_acc_e), .out_21(C),
    .ALU_0(cpu_control_section_4b4a8754_1_alu_0), .ALU_1(cpu_control_section_4b4a8754_1_alu_1),
    .ALU_2(cpu_control_section_4b4a8754_1_alu_2),
    .BUS_1_0aec77e3(cpu_control_section_4b4a8754_1_bus_1_0aec77e3),
    .IAR_E(cpu_control_section_4b4a8754_1_iar_e), .IO_CLK_E_8c330f33(E));
  CPU_R cpu_r_1 (
    .i(BUS_OUTPUT_8a49af3e), .s(cpu_control_section_4b4a8754_1_r0_s),
    .e(cpu_control_section_4b4a8754_1_r0_e), .\reg (R0), .o(BUS_OUTPUT_8a49af3e));
  CPU_R cpu_r_2 (
    .i(BUS_OUTPUT_8a49af3e), .s(cpu_control_section_4b4a8754_1_r1_s),
    .e(cpu_control_section_4b4a8754_1_r1_e), .\reg (R1), .o(BUS_OUTPUT_8a49af3e));
  CPU_IAR cpu_iar_1 (
    .i(BUS_OUTPUT_8a49af3e), .s(cpu_control_section_4b4a8754_1_iar_s),
    .e(cpu_control_section_4b4a8754_1_iar_e), .IAR(out_19), .o(BUS_OUTPUT_8a49af3e));
  CPU_R cpu_r_3 (
    .i(BUS_OUTPUT_8a49af3e), .s(cpu_control_section_4b4a8754_1_r2_s),
    .e(cpu_control_section_4b4a8754_1_r2_e), .\reg (R2), .o(BUS_OUTPUT_8a49af3e));
  CPU_IR cpu_ir_1 (.i(BUS_OUTPUT_8a49af3e), .s(cpu_control_section_4b4a8754_1_ir_s), .o(out_18));
  CPU_R cpu_r_4 (
    .i(BUS_OUTPUT_8a49af3e), .s(cpu_control_section_4b4a8754_1_r3_s),
    .e(cpu_control_section_4b4a8754_1_r3_e), .\reg (R3), .o(BUS_OUTPUT_8a49af3e));
  Multiplexer #(.enable("true"), .width(8)) multiplexer_1 (
    .in0(BUS_OUTPUT_8a49af3e), .in1(RAM_INPUT_ad5b00f9), .out(multiplexer_1_out), .sel(LOAD));  // open: en
  CPU_RAM_256 cpu_ram_256_1 (
    .address(BUS_OUTPUT_8a49af3e), .reset(RESET), .i(multiplexer_1_out),
    .s(cpu_control_section_4b4a8754_1_ram_s), .e(cpu_control_section_4b4a8754_1_ram_e),
    .sa(cpu_control_section_4b4a8754_1_mar_s), .L_56_a274d823(cpu_ram_256_1_l_56_a274d823),
    .L_55_09b2a5b5(cpu_ram_256_1_l_56_a274d823), .o(BUS_OUTPUT_8a49af3e));  // open: L_107_afc376ab, L_123_a49b0d68, L_139_8f550c1a, L_155_0fb7c184, L_171_afa03cad, L_187_525802f1, L_203_bcbe93e4, L_219_5e44a710, L_11_d9827db8, L_235_eba3b9a0, L_251_ff78a34a, L_27_6ee616b1, L_43_5cd73d77, L_59_5187825b, L_75_6762c5d7, L_91_e4fec703, L_106_890633e3, L_122_d75ac8bc, L_138_97eda11e, L_154_95c69e8f, L_170_a17084e7, L_186_0846180c, L_202_82cf4e1e, L_218_4e23f89b, L_10_884b6e1b, L_234_53f3880a, L_250_f097ffeb, L_26_60793931, L_42_4597cfe2, L_58_cc0e5230, L_74_b7af5351, L_90_87ff629e, L_105_ec1bd0aa, L_121_67e46722, L_137_0a3513b3, L_153_cbdf0bd1, L_169_b063b05b, L_185_1eff2a27, L_201_bd709e47, L_217_c14910f1, L_9_e63877d4, L_233_38dcf616, L_249_d979fe68, L_25_edd3a926, L_41_1d3782fe, L_57_b8cf3fac, L_73_dfdb2ca0, L_89_379e7e7e, L_104_9a2c499d, L_120_34b6a3ba, L_136_546f722a, L_152_e0fd29c5, L_168_3e5d9c10, L_184_3b6ae0be, L_200_ad9398b8, L_216_e5257089, L_8_0263bcbb, L_232_a6252b72, L_248_52e87327, L_24_60803382, L_40_4ca6ce3b, L_72_0f3ff63b, L_88_441b4085, L_103_4ca9a9e8, L_119_83e16f30, L_135_9f7935da, L_151_c137f5fb, L_167_583d80af, L_183_d7d3aedc, L_199_7a2c8e8c, L_215_2db12d0c, L_7_21e06148, L_231_a0aa18c3, L_247_03de5ec1, L_23_5bebf840, L_39_a919e418, L_71_7a7bc430, L_87_afa8acd5, L_102_dee4d37a, L_118_35745232, L_134_596005b2, L_150_7c684449, L_166_6ce6b1d2, L_182_06695f08, L_198_e3703de4, L_214_d5e83083, L_6_35fe27e4, L_230_079eec06, L_246_f29b66c1, L_22_3fa04d94, L_38_9f366372, L_54_7adb3ac6, L_70_4c14f7ed, L_86_50a3a49b, L_101_4b0585e7, L_117_37beb9f1, L_133_f4ed92b5, L_149_aedbc0dc, L_165_4b39f19f, L_181_0ab10fed, L_197_a5dcd0c4, L_213_4c7eba85, L_5_5a09c7b9, L_229_5e73c8ec, L_245_61a52dc4, L_21_2793d292, L_37_b49ff5fb, L_53_e0194783, L_69_b6eb8b05, L_85_e1dcb90a, L_100_8c031f7c, L_116_eb4bf423, L_132_b753a49c, L_148_2805e3d8, L_164_e3ad4dcd, L_180_02f18e6e, L_196_0df3d184, L_212_8a2a5a8d, L_4_df9eb970, L_228_2780ed2a, L_244_379bb360, L_20_b0f18e1f, L_36_5c9707bd, L_52_39705d0b, L_68_24398868, L_84_7571b0a3, L_99_754ffd2e, L_115_378b6fa7, L_131_07e5c019, L_147_486cfd5e, L_163_f1205ac3, L_179_73e91140, L_195_b21ea119, L_211_e9340d09, out_20, L_227_5e0a05c8, L_243_9f608c5c, L_19_df0ab950, L_35_a8d555d1, L_51_8e7c53d8, L_67_7dd7fcd5, L_83_0ffa05ff, L_98_4126bf5f, L_114_10d15639, L_130_edf1f25b, L_146_6e9a62c2, L_162_378193de, L_178_32520e06, L_194_a892d091, L_210_32305997, L_2_021c411d, L_226_50d65f3a, L_242_1ddb9925, L_18_77c23569, L_34_198975c3, L_50_30e7a076, L_66_c6e314cf, L_82_f95cee65, L_97_edb68727, L_113_4fe9915b, L_129_8f4b512c, L_145_c25a15c7, L_161_8d58ff55, L_177_376295cf, L_193_b6a4fb0e, L_209_cc1e9a99, L_1_a0dbb3e4, L_225_3caf72b0, L_241_6d61ff0f, L_17_a6f2001c, L_33_b87346dc, L_49_9d69905f, L_65_f777b26e, L_81_192bbbc9, L_96_b42dc9a0, L_112_0ffd8e77, L_128_beedcbc0, L_144_ec1a4d9d, L_160_30e8e70a, L_176_e00acc67, L_192_966b3b1b, L_208_04a30dd2, L_0_0718cde6, L_224_8b1b15a3, L_240_a5ae4278, L_16_4a4ef9fa, L_32_b3d84c07, L_48_cd210754, L_64_38ccf0ea, L_80_f25c8b42, L_111_5b0b1347, L_127_603c7aaf, L_143_3745504f, L_159_438416df, L_175_5fd8dca1, L_191_42c30af8, L_207_d9596663, L_223_1c13ccba, L_15_49b3f215, L_239_932bc3e8, L_255_715f482c, L_31_244d0c43, L_47_4b05a2a0, L_63_9b5c08e1, L_79_65da426e, L_95_ef83c9fc, L_110_5061371d, L_126_ab782779, L_142_6af56551, L_158_a8dd2cd8, L_174_3938b5d2, L_190_be8c7ea7, L_206_beee4402, L_222_e33a5884, L_14_09a57ae2, L_238_db4eae34, L_254_22eeae1a, L_30_8aab3891, L_46_1b94c33f, L_62_d1b1203b, L_78_c15dfd7a, L_94_e033720c, L_109_49389abb, L_125_d87b9d02, L_141_bdf5edb1, L_157_3025f0db, L_173_868f5f47, L_189_2ca3d932, L_205_56d0b0a5, L_221_982e7a40, L_13_b05b92d5, L_237_9847a8d5, L_253_0a063966, L_29_20ac879c, L_45_4e81981e, L_61_c72da5da, L_77_c0c0c278, L_93_734946e0, L_108_0c1b67c6, L_124_5c6a63bc, L_140_efb15ed6, L_156_579de1cf, L_172_84c173cb, L_188_0c7598d3, L_204_508e99d4, L_220_7c2af14b, L_12_d8925d08, L_236_fb6b3f93, L_252_f85afb85, L_28_887e6408, L_44_455ab579, L_60_007aac1b, L_76_0dd232d6, L_92_92986eb9

  // Notes on the sheet:
  //   BUS_OUTPUT_8a49af3e: pull=down
endmodule

module CPU_IAR (
  input  [7:0] i,
  input  s,
  input  e,
  output [7:0] IAR,
  output [7:0] o
);

  CPU_REGISTER_8 cpu_register_8_1 (.i(i), .s(s), .e(e), .REG(IAR), .L_0_0718cde6(o));

  // Notes on the sheet:
  //   i: pull=down
  //   s: pull=down
  //   e: pull=down
  //   o: pull=down
endmodule

module CPU_IR (
  input  [7:0] i,
  input  s,
  output [7:0] o
);

  CPU_MEM_8 cpu_mem_8_1 (.in_1(i), .s(s), .out_3(o));

  // Notes on the sheet:
  //   i: pull=down
  //   s: pull=down
  //   o: pull=down
endmodule

module CPU_FLAGS (
  input  C,
  input  A,
  input  E,
  input  Z,
  input  s,
  output out_6,
  output out_7,
  output out_8,
  output out_9
);

  CPU_MEM_1 cpu_mem_1_1 (.in_2(s), .in_1(C), .out_3(out_6));
  CPU_MEM_1 cpu_mem_1_2 (.in_2(s), .in_1(A), .out_3(out_7));
  CPU_MEM_1 cpu_mem_1_3 (.in_2(s), .in_1(E), .out_3(out_8));
  CPU_MEM_1 cpu_mem_1_4 (.in_2(s), .in_1(Z), .out_3(out_9));

  // Notes on the sheet:
  //   C: pull=down
  //   A: pull=down
  //   E: pull=down
  //   Z: pull=down
  //   out_6: pull=down
  //   out_7: pull=down
  //   out_8: pull=down
  //   out_9: pull=down
endmodule

module CPU_CONTROL_SECTION_4b4a8754 (
  input  clks,
  input  clk,
  input  clke,
  input  LOAD,
  input  MARS,
  input  RESET,
  input  C,
  input  A,
  input  E,
  input  Z,
  input  [7:0] IR_IN_c6fa6e43,
  output BUS_1_0aec77e3,
  output IR_S,
  output MAR_S,
  output IAR_E,
  output IAR_S,
  output RAM_E,
  output ACC_S,
  output ACC_E,
  output RAM_S,
  output out_21,
  output TMP_S,
  output IO_CLK_E_8c330f33,
  output FLAGS_S,
  output IO_CLKS_S_d3c82ef0,
  output R0_S,
  output R0_E,
  output R1_S,
  output R1_E,
  output R2_E,
  output R2_S,
  output R3_E,
  output R3_S,
  output END,
  output IO,
  output DA,
  output ALU_0,
  output ALU_1,
  output ALU_2
);

  wire and_5_out, and_6_out, and_7_out, and_8_out, and_9_out, and_10_out, and_11_out, and_12_out, and_16_out,
       and_17_out, and_18_out, and_19_out, and_20_out, and_21_out, and_22_out, and_23_out, and_24_out,
       and_25_out, and_26_out, and_27_out, and_28_out, and_29_out, and_30_out, and_31_out, and_32_out,
       and_33_out, and_34_out, and_35_out, and_36_out, and_37_out, and_38_out, and_39_out, and_42_out,
       and_43_out, and_44_out, and_45_out, and_46_out, and_47_out, and_48_out, and_49_out, and_50_out,
       and_51_out, and_52_out, and_53_out, and_54_out, and_55_out, and_56_out, and_57_out, and_58_out,
       and_60_out, and_61_out, and_62_out, and_63_out, cpu_decoder_2x4_1_l_0_0718cde6,
       cpu_decoder_2x4_1_l_1_a0dbb3e4, cpu_decoder_2x4_1_l_2_021c411d, cpu_decoder_2x4_1_l_3_eef39203,
       cpu_decoder_2x4_west_1_l_0_0718cde6, cpu_decoder_2x4_west_1_l_1_a0dbb3e4,
       cpu_decoder_2x4_west_1_l_2_021c411d, cpu_decoder_2x4_west_1_l_3_eef39203,
       cpu_decoder_2x4_west_2_l_0_0718cde6, cpu_decoder_2x4_west_2_l_1_a0dbb3e4,
       cpu_decoder_2x4_west_2_l_2_021c411d, cpu_decoder_2x4_west_2_l_3_eef39203,
       cpu_decoder_cntrl_3x8_1_l_0_0718cde6, cpu_decoder_cntrl_3x8_1_l_1_a0dbb3e4,
       cpu_decoder_cntrl_3x8_1_l_2_021c411d, cpu_decoder_cntrl_3x8_1_l_3_eef39203,
       cpu_decoder_cntrl_3x8_1_l_4_df9eb970, cpu_decoder_cntrl_3x8_1_l_5_5a09c7b9,
       cpu_decoder_cntrl_3x8_1_l_6_35fe27e4, cpu_decoder_cntrl_3x8_1_l_7_21e06148,
       cpu_stepper_1_step_1_4896c425, cpu_stepper_1_step_2_d28dd23a, cpu_stepper_1_step_3_5d5bb038,
       cpu_stepper_1_step_4_6f30b4e7, cpu_stepper_1_step_5_fb56fd61, cpu_stepper_1_step_6_3a46c3ff,
       cpu_stepper_1_step_7_7823715d, not_1_out, not_2_out, not_3_out, not_4_out, not_5_out, not_6_out,
       not_7_out, or_6_out, or_7_out, or_8_out, or_9_out, or_10_out, or_11_out, or_12_out, or_13_out,
       or_14_out, or_15_out, or_16_out;

  and and_1 (IAR_E, clke, or_6_out);
  and and_2 (RAM_E, clke, or_7_out);
  and and_3 (ACC_E, clke, or_8_out);
  and and_4 (IO_CLK_E_8c330f33, clke, and_47_out);
  or or_1 (R0_E, and_5_out, and_9_out);
  or or_2 (R1_E, and_6_out, and_10_out);
  or or_3 (R2_E, and_7_out, and_11_out);
  or or_4 (R3_E, and_8_out, and_12_out);
  and and_5 (and_5_out, clke, or_9_out, cpu_decoder_2x4_west_1_l_0_0718cde6);
  and and_6 (and_6_out, clke, or_9_out, cpu_decoder_2x4_west_1_l_1_a0dbb3e4);
  and and_7 (and_7_out, clke, or_9_out, cpu_decoder_2x4_west_1_l_2_021c411d);
  and and_8 (and_8_out, clke, or_9_out, cpu_decoder_2x4_west_1_l_3_eef39203);
  and and_9 (and_9_out, clke, or_10_out, cpu_decoder_2x4_west_2_l_0_0718cde6);
  and and_10 (and_10_out, clke, or_10_out, cpu_decoder_2x4_west_2_l_1_a0dbb3e4);
  and and_11 (and_11_out, clke, or_10_out, cpu_decoder_2x4_west_2_l_2_021c411d);
  and and_12 (and_12_out, clke, or_10_out, cpu_decoder_2x4_west_2_l_3_eef39203);
  and and_13 (ALU_0, cpu_stepper_1_step_5_fb56fd61, IR_IN_c6fa6e43[7], IR_IN_c6fa6e43[4]);
  and and_14 (ALU_1, cpu_stepper_1_step_5_fb56fd61, IR_IN_c6fa6e43[7], IR_IN_c6fa6e43[5]);
  and and_15 (ALU_2, cpu_stepper_1_step_5_fb56fd61, IR_IN_c6fa6e43[7], IR_IN_c6fa6e43[6]);
  or or_5 (BUS_1_0aec77e3, and_17_out, and_38_out, and_37_out, and_34_out);
  or or_6 (or_6_out, and_17_out, and_34_out, and_36_out, and_37_out);
  or or_7 (or_7_out, cpu_stepper_1_step_2_d28dd23a, and_42_out);
  or or_8 (or_8_out, cpu_stepper_1_step_3_5d5bb038, and_46_out, and_49_out, and_48_out);
  or or_9 (or_9_out, and_31_out, and_43_out, and_35_out, and_39_out);
  or or_10 (or_10_out, and_33_out, and_32_out, out_21);
  and and_16 (and_16_out, clk, not_1_out);
  not not_1 (not_1_out, LOAD);
  not not_2 (not_2_out, LOAD);
  CPU_DECODER_2x4_WEST cpu_decoder_2x4_west_1 (
    .a(IR_IN_c6fa6e43[0]), .b(IR_IN_c6fa6e43[1]), .L_0_0718cde6(cpu_decoder_2x4_west_1_l_0_0718cde6),
    .L_1_a0dbb3e4(cpu_decoder_2x4_west_1_l_1_a0dbb3e4), .L_2_021c411d(cpu_decoder_2x4_west_1_l_2_021c411d),
    .L_3_eef39203(cpu_decoder_2x4_west_1_l_3_eef39203));
  CPU_DECODER_2x4_WEST cpu_decoder_2x4_west_2 (
    .a(IR_IN_c6fa6e43[2]), .b(IR_IN_c6fa6e43[3]), .L_0_0718cde6(cpu_decoder_2x4_west_2_l_0_0718cde6),
    .L_1_a0dbb3e4(cpu_decoder_2x4_west_2_l_1_a0dbb3e4), .L_2_021c411d(cpu_decoder_2x4_west_2_l_2_021c411d),
    .L_3_eef39203(cpu_decoder_2x4_west_2_l_3_eef39203));
  CPU_STEPPER cpu_stepper_1 (
    .clk(and_16_out), .reset(cpu_stepper_1_step_7_7823715d), .step_4_6f30b4e7(cpu_stepper_1_step_4_6f30b4e7),
    .step_5_fb56fd61(cpu_stepper_1_step_5_fb56fd61), .step_6_3a46c3ff(cpu_stepper_1_step_6_3a46c3ff),
    .step_7_7823715d(cpu_stepper_1_step_7_7823715d), .step_1_4896c425(cpu_stepper_1_step_1_4896c425),
    .step_2_d28dd23a(cpu_stepper_1_step_2_d28dd23a), .step_3_5d5bb038(cpu_stepper_1_step_3_5d5bb038));
  and and_17 (and_17_out, not_2_out, cpu_stepper_1_step_1_4896c425);
  not not_3 (not_3_out, IR_IN_c6fa6e43[7]);
  CPU_DECODER_CNTRL_3x8 cpu_decoder_cntrl_3x8_1 (
    .c(IR_IN_c6fa6e43[4]), .a(IR_IN_c6fa6e43[6]), .b(IR_IN_c6fa6e43[5]),
    .L_0_0718cde6(cpu_decoder_cntrl_3x8_1_l_0_0718cde6), .L_1_a0dbb3e4(cpu_decoder_cntrl_3x8_1_l_1_a0dbb3e4),
    .L_2_021c411d(cpu_decoder_cntrl_3x8_1_l_2_021c411d), .L_3_eef39203(cpu_decoder_cntrl_3x8_1_l_3_eef39203),
    .L_4_df9eb970(cpu_decoder_cntrl_3x8_1_l_4_df9eb970), .L_5_5a09c7b9(cpu_decoder_cntrl_3x8_1_l_5_5a09c7b9),
    .L_6_35fe27e4(cpu_decoder_cntrl_3x8_1_l_6_35fe27e4), .L_7_21e06148(cpu_decoder_cntrl_3x8_1_l_7_21e06148));
  and and_18 (and_18_out, not_3_out, cpu_decoder_cntrl_3x8_1_l_0_0718cde6);
  and and_19 (and_19_out, not_3_out, cpu_decoder_cntrl_3x8_1_l_1_a0dbb3e4);
  and and_20 (and_20_out, not_3_out, cpu_decoder_cntrl_3x8_1_l_2_021c411d);
  and and_21 (and_21_out, not_3_out, cpu_decoder_cntrl_3x8_1_l_3_eef39203);
  and and_22 (and_22_out, not_3_out, cpu_decoder_cntrl_3x8_1_l_4_df9eb970);
  and and_23 (and_23_out, not_3_out, cpu_decoder_cntrl_3x8_1_l_5_5a09c7b9);
  and and_24 (and_24_out, not_3_out, cpu_decoder_cntrl_3x8_1_l_6_35fe27e4);
  and and_25 (and_25_out, not_3_out, cpu_decoder_cntrl_3x8_1_l_7_21e06148);
  not not_4 (not_4_out, IR_IN_c6fa6e43[5]);
  not not_5 (not_5_out, IR_IN_c6fa6e43[4]);
  and and_26 (and_26_out, C, IR_IN_c6fa6e43[3]);
  and and_27 (and_27_out, A, IR_IN_c6fa6e43[2]);
  and and_28 (and_28_out, E, IR_IN_c6fa6e43[1]);
  and and_29 (and_29_out, Z, IR_IN_c6fa6e43[0]);
  or or_11 (or_11_out, and_26_out, and_27_out, and_28_out, and_29_out);
  and and_30 (and_30_out, IR_IN_c6fa6e43[4], IR_IN_c6fa6e43[5], IR_IN_c6fa6e43[6]);
  not not_6 (not_6_out, and_30_out);
  and and_31 (and_31_out, cpu_stepper_1_step_4_6f30b4e7, IR_IN_c6fa6e43[7]);
  and and_32 (and_32_out, cpu_stepper_1_step_4_6f30b4e7, and_18_out);
  and and_33 (and_33_out, cpu_stepper_1_step_4_6f30b4e7, and_19_out);
  and and_34 (and_34_out, cpu_stepper_1_step_4_6f30b4e7, and_20_out);
  and and_35 (and_35_out, cpu_stepper_1_step_4_6f30b4e7, and_21_out);
  and and_36 (and_36_out, cpu_stepper_1_step_4_6f30b4e7, and_22_out);
  and and_37 (and_37_out, cpu_stepper_1_step_4_6f30b4e7, and_23_out);
  and and_38 (and_38_out, cpu_stepper_1_step_4_6f30b4e7, and_24_out);
  and and_39 (and_39_out, cpu_stepper_1_step_4_6f30b4e7, and_25_out, IR_IN_c6fa6e43[3]);
  and and_40 (END, IR_IN_c6fa6e43[7], IR_IN_c6fa6e43[6], not_4_out, not_5_out, cpu_stepper_1_step_4_6f30b4e7, IR_IN_c6fa6e43[3], IR_IN_c6fa6e43[2], IR_IN_c6fa6e43[1], IR_IN_c6fa6e43[0]);
  and and_41 (out_21, cpu_stepper_1_step_5_fb56fd61, IR_IN_c6fa6e43[7]);
  and and_42 (and_42_out, cpu_stepper_1_step_5_fb56fd61, and_18_out);
  and and_43 (and_43_out, cpu_stepper_1_step_5_fb56fd61, and_19_out);
  and and_44 (and_44_out, cpu_stepper_1_step_5_fb56fd61, and_20_out);
  and and_45 (and_45_out, cpu_stepper_1_step_5_fb56fd61, and_22_out);
  and and_46 (and_46_out, cpu_stepper_1_step_5_fb56fd61, and_23_out);
  not not_7 (not_7_out, IR_IN_c6fa6e43[3]);
  and and_47 (and_47_out, cpu_stepper_1_step_5_fb56fd61, and_25_out, not_7_out);
  and and_48 (and_48_out, cpu_stepper_1_step_6_3a46c3ff, IR_IN_c6fa6e43[7], not_6_out);
  and and_49 (and_49_out, cpu_stepper_1_step_6_3a46c3ff, and_20_out);
  and and_50 (and_50_out, cpu_stepper_1_step_6_3a46c3ff, and_23_out, or_11_out);
  CPU_DECODER_2x4 cpu_decoder_2x4_1 (
    .a(IR_IN_c6fa6e43[0]), .b(IR_IN_c6fa6e43[1]), .L_0_0718cde6(cpu_decoder_2x4_1_l_0_0718cde6),
    .L_1_a0dbb3e4(cpu_decoder_2x4_1_l_1_a0dbb3e4), .L_2_021c411d(cpu_decoder_2x4_1_l_2_021c411d),
    .L_3_eef39203(cpu_decoder_2x4_1_l_3_eef39203));
  or or_12 (or_12_out, and_17_out, and_34_out, and_37_out, and_32_out, and_33_out, and_36_out);
  or or_13 (or_13_out, cpu_stepper_1_step_3_5d5bb038, and_35_out, and_46_out, and_45_out, and_49_out, and_50_out);
  or or_14 (or_14_out, and_17_out, and_34_out, and_37_out, out_21);
  or or_15 (or_15_out, and_38_out, out_21);
  or or_16 (or_16_out, and_42_out, and_48_out, and_44_out, and_47_out);
  and and_51 (and_51_out, clks, cpu_stepper_1_step_2_d28dd23a);
  and and_52 (and_52_out, clks, or_12_out);
  and and_53 (and_53_out, clks, or_13_out);
  and and_54 (and_54_out, clks, or_14_out);
  and and_55 (and_55_out, LOAD, clks);
  and and_56 (and_56_out, clks, and_43_out);
  and and_57 (and_57_out, clks, and_31_out);
  and and_58 (and_58_out, clks, or_15_out);
  and and_59 (IO_CLKS_S_d3c82ef0, clks, and_39_out);
  and and_60 (and_60_out, clks, or_16_out, cpu_decoder_2x4_1_l_0_0718cde6);
  and and_61 (and_61_out, clks, or_16_out, cpu_decoder_2x4_1_l_1_a0dbb3e4);
  and and_62 (and_62_out, clks, or_16_out, cpu_decoder_2x4_1_l_2_021c411d);
  and and_63 (and_63_out, clks, or_16_out, cpu_decoder_2x4_1_l_3_eef39203);
  or or_17 (IR_S, RESET, and_51_out);
  or or_18 (MAR_S, MARS, and_52_out);
  or or_19 (IAR_S, RESET, and_53_out);
  or or_20 (ACC_S, RESET, and_54_out);
  or or_21 (RAM_S, and_55_out, and_56_out);
  or or_22 (TMP_S, RESET, and_57_out);
  or or_23 (FLAGS_S, RESET, and_58_out);
  or or_24 (R0_S, RESET, and_60_out);
  or or_25 (R1_S, RESET, and_61_out);
  or or_26 (R2_S, RESET, and_62_out);
  or or_27 (R3_S, RESET, and_63_out);

  assign DA = IR_IN_c6fa6e43[3];
  assign IO = IR_IN_c6fa6e43[2];

  // Notes on the sheet:
  //   REG B_E
  //   REG A
  //   REG B
  //   REG A
  //   REG B_S
endmodule

module CPU_CLK (
  input  clkin,
  output clk,
  output clks,
  output clke
);

  wire j_k_ff_1_qn, nand_1_out;

  J_K_Flip_Flop j_k_ff_1 (.J(1'b1), .clk(clkin), .K(1'b1), .Q(clk), .Qn(j_k_ff_1_qn));  // open: preset, reset
  nand nand_1 (nand_1_out, clkin, clk);
  nand nand_2 (clke, j_k_ff_1_qn, clkin);
  not not_1 (clks, nand_1_out);

  // Notes on the sheet:
  //   clkin: pull=down
  //   clk: pull=down
  //   clks: pull=down
  //   clke: pull=down
endmodule

module CPU_DECODER_2x4 (
  input  a,
  input  b,
  output L_0_0718cde6,
  output L_1_a0dbb3e4,
  output L_2_021c411d,
  output L_3_eef39203
);

  wire not_1_out, not_2_out;

  not not_1 (not_1_out, b);
  not not_2 (not_2_out, a);
  and and_1 (L_0_0718cde6, not_2_out, not_1_out);
  and and_2 (L_1_a0dbb3e4, a, not_1_out);
  and and_3 (L_2_021c411d, b, not_2_out);
  and and_4 (L_3_eef39203, b, a);

  // Notes on the sheet:
  //   a: pull=down
  //   b: pull=down
endmodule

module CPU_DECODER_2x4_WEST (
  input  a,
  input  b,
  output L_0_0718cde6,
  output L_1_a0dbb3e4,
  output L_2_021c411d,
  output L_3_eef39203
);

  wire not_1_out, not_2_out;

  not not_1 (not_1_out, b);
  not not_2 (not_2_out, a);
  and and_1 (L_0_0718cde6, not_2_out, not_1_out);
  and and_2 (L_1_a0dbb3e4, a, not_1_out);
  and and_3 (L_2_021c411d, b, not_2_out);
  and and_4 (L_3_eef39203, b, a);

  // Notes on the sheet:
  //   a: pull=down
  //   b: pull=down
endmodule

module CPU_DECODER_CNTRL_3x8 (
  input  a,
  input  b,
  input  c,
  output L_0_0718cde6,
  output L_1_a0dbb3e4,
  output L_2_021c411d,
  output L_3_eef39203,
  output L_4_df9eb970,
  output L_5_5a09c7b9,
  output L_6_35fe27e4,
  output L_7_21e06148
);

  wire not_1_out, not_2_out, not_3_out;

  not not_1 (not_1_out, c);
  not not_2 (not_2_out, b);
  not not_3 (not_3_out, a);
  and and_1 (L_0_0718cde6, not_3_out, not_2_out, not_1_out);
  and and_2 (L_1_a0dbb3e4, not_3_out, not_2_out, c);
  and and_3 (L_2_021c411d, not_3_out, b, not_1_out);
  and and_4 (L_3_eef39203, not_3_out, b, c);
  and and_5 (L_4_df9eb970, a, not_2_out, not_1_out);
  and and_6 (L_5_5a09c7b9, a, not_2_out, c);
  and and_7 (L_6_35fe27e4, a, b, not_1_out);
  and and_8 (L_7_21e06148, a, b, c);

  // Notes on the sheet:
  //   c: pull=down
  //   a: pull=down
  //   b: pull=down
endmodule

module CPU_TEST (
  input  LOAD,
  input  MARS
);

  wire CLK, CLKE, CLKL, CLKS, END, RESET;
  wire [7:0] ACC, BUS, IAR, IR, load_256_count_1_count, R0, R1, R2, R3, RAM_INPUT_ad5b00f9;

  Hex_Digit_Display hex_digit_display_1 (.value(BUS[7:4]));  // open: dp
  CPU cpu_1 (
    .RAM_INPUT_ad5b00f9(RAM_INPUT_ad5b00f9), .MARS(MARS), .LOAD(LOAD), .clock(CLK), .RESET(RESET),
    .out_18(IR), .R2(R2), .R3(R3), .END(END), .out_20(ACC), .clkl(CLKL), .clke(CLKE), .clks(CLKS), .R0(R0),
    .BUS_OUTPUT_8a49af3e(BUS), .out_19(IAR), .R1(R1));  // open: S, E, IO, DA
  Hex_Digit_Display hex_digit_display_2 (.value(BUS[3:0]));  // open: dp
  LOAD_256_COUNT load_256_count_1 (.clk(CLKL), .count(load_256_count_1_count));  // open: carry
  Hex_Digit_Display hex_digit_display_3 (.value(ACC[7:4]));  // open: dp
  Hex_Digit_Display hex_digit_display_4 (.value(ACC[3:0]));  // open: dp
  RAM ram_1 (.addr(load_256_count_1_count), .data(RAM_INPUT_ad5b00f9), .sel(LOAD), .clk(CLKL), .ld(1'b1), .clr(1'b0));
  Hex_Digit_Display hex_digit_display_5 (.value(IAR[7:4]));  // open: dp
  Hex_Digit_Display hex_digit_display_6 (.value(IAR[3:0]));  // open: dp
  Hex_Digit_Display hex_digit_display_7 (.value(IR[7:4]));  // open: dp
  Hex_Digit_Display hex_digit_display_8 (.value(IR[3:0]));  // open: dp
  Hex_Digit_Display hex_digit_display_9 (.value(R0[7:4]));  // open: dp
  Hex_Digit_Display hex_digit_display_10 (.value(R0[3:0]));  // open: dp
  Hex_Digit_Display hex_digit_display_11 (.value(R1[3:0]));  // open: dp
  Hex_Digit_Display hex_digit_display_12 (.value(R1[7:4]));  // open: dp
  Button u_RESET (.out(RESET));
  LED #(.active("false")) led_1 (.in(END));
  Clock u_CLK (.out(CLK));
  Hex_Digit_Display hex_digit_display_13 (.value(R2[7:4]));  // open: dp
  Hex_Digit_Display hex_digit_display_14 (.value(R2[3:0]));  // open: dp
  Hex_Digit_Display hex_digit_display_15 (.value(R3[7:4]));  // open: dp
  Hex_Digit_Display hex_digit_display_16 (.value(R3[3:0]));  // open: dp

  // Notes on the sheet:
  //   BUS
  //   ACC
  //   EXTERNAL RAM
  //   IAR
  //   IR
  //   RO
  //   1 -
  //   2 -
  //   3 -
  //   0
  //   1
  //   0
  //   R1
  //   R2
  //   R3
endmodule

module CPU_CARRY_TEMP (
  input  c,
  input  s,
  output o
);

  CPU_MEM_1 cpu_mem_1_1 (.in_2(s), .in_1(c), .out_3(o));
endmodule

module LOAD_256_COUNT (
  input  clk,
  output [7:0] count,
  output carry
);

  wire counter_1_carry;

  Counter #(.ongoal("stay"), .trigger("falling")) counter_1 (
    .count(1'b1), .Q(count), .carry(counter_1_carry), .clk(clk));  // open: load, D, up, clr
  not not_1 (carry, counter_1_carry);
endmodule

module CPU_DELAY (
  input  [7:0] i,
  input  clk,
  output [7:0] o
);

  Counter #(.ongoal("stay"), .trigger("falling")) counter_1 (
    .load(1'b1), .D(i), .count(1'b0), .Q(o), .clk(clk));  // open: carry, up, clr
endmodule
