// Logisim project active_high_with_enable.circ as structural Verilog: 1 circuit, main circuit main
module main (
  input  s,
  input  e,
  output q
);

  wire nand_1_out, nand_2_out, nand_4_out, not_1_out;

  not not_1 (not_1_out, s);
  nand nand_1 (nand_1_out, s, e);
  nand nand_2 (nand_2_out, e, not_1_out);
  nand nand_3 (q, nand_1_out, nand_4_out);
  nand nand_4 (nand_4_out, q, nand_2_out);

  // Notes on the sheet:
  //   Active High with Enable
endmodule
