// Logisim project active_low_sr_latch.circ as structural Verilog: 1 circuit, main circuit main
module main (
  input  s,
  input  r,
  output q,
  output nq
);

  nand nand_1 (q, s, nq);
  nand nand_2 (nq, q, r);

  // Notes on the sheet:
  //   Active Low S R Latch
endmodule
