// Logisim project eight_bit_memory_cell.circ as structural Verilog: 6 circuits, main circuit main
module main (
);

  CPU_REG_8 cpu_reg_8_1 ();  // open: in_1, in_2, in_3, out_4
  Mem_Cell mem_cell_1 ();  // open: in_1, in_2, in_3, out_4, out_5
endmodule

module CPU_MEM_1 (
  input  s,
  input  e,
  output q
);

  wire nand_1_out, nand_2_out, nand_4_out;

  nand nand_1 (nand_1_out, s, e);
  nand nand_2 (nand_2_out, e, nand_1_out);
  nand nand_3 (q, nand_1_out, nand_4_out);
  nand nand_4 (nand_4_out, q, nand_2_out);

  // Notes on the sheet:
  //   1 bit memory cell
endmodule

module CPU_MEM_8 (
  input  [7:0] in_1,
  input  in_2,
  output [7:0] out_3
);

  CPU_MEM_1 cpu_mem_1_1 (.s(in_1[0]), .e(in_2), .q(out_3[0]));
  CPU_MEM_1 cpu_mem_1_2 (.s(in_1[1]), .e(in_2), .q(out_3[1]));
  CPU_MEM_1 cpu_mem_1_3 (.s(in_1[2]), .e(in_2), .q(out_3[2]));
  CPU_MEM_1 cpu_mem_1_4 (.s(in_1[3]), .e(in_2), .q(out_3[3]));
  CPU_MEM_1 cpu_mem_1_5 (.s(in_1[4]), .e(in_2), .q(out_3[4]));
  CPU_MEM_1 cpu_mem_1_6 (.s(in_1[5]), .e(in_2), .q(out_3[5]));
  CPU_MEM_1 cpu_mem_1_7 (.s(in_1[6]), .e(in_2), .q(out_3[6]));
  CPU_MEM_1 cpu_mem_1_8 (.s(in_1[7]), .e(in_2), .q(out_3[7]));
endmodule

module CPU_ENABLE (
  input  [7:0] in_1,
  input  in_2,
  output [7:0] out_3
);

  and and_1 (out_3[0], in_1[0], in_2);
  and and_2 (out_3[1], in_1[1], in_2);
  and and_3 (out_3[2], in_1[2], in_2);
  and and_4 (out_3[3], in_1[3], in_2);
  and and_5 (out_3[4], in_1[4], in_2);
  and and_6 (out_3[5], in_1[5], in_2);
  and and_7 (out_3[6], in_1[6], in_2);
  and and_8 (out_3[7], in_1[7], in_2);
endmodule

module CPU_REG_8 (
  input  [7:0] in_1,
  input  in_2,
  input  in_3,
  output [7:0] out_4
);

  wire [7:0] cpu_mem_8_1_out_3;

  CPU_MEM_8 cpu_mem_8_1 (.in_1(in_1), .in_2(in_2), .out_3(cpu_mem_8_1_out_3));
  CPU_ENABLE cpu_enable_1 (.in_1(cpu_mem_8_1_out_3), .in_2(in_3), .out_3(out_4));
endmodule

module Mem_Cell (
  input  [7:0] in_1,
  input  in_2,
  input  in_3,
  output [7:0] out_4,
  output [7:0] out_5
);

  wire [7:0] cpu_enable_1_out_3;

  CPU_MEM_8 cpu_mem_8_1 (.in_1(in_1), .in_2(in_2), .out_3(out_4));
  assign out_5 = in_3 ? cpu_enable_1_out_3 : 8'bz;  // Controlled_Buffer controlled_buffer_1
  CPU_ENABLE cpu_enable_1 (.in_1(out_4), .in_2(in_3), .out_3(cpu_enable_1_out_3));
endmodule
