// Logisim project one_bit_memory_cell.circ as structural Verilog: 2 circuits, main circuit main
module main (
  input  s,
  input  e,
  output q
);

  wire nand_1_out, nand_2_out, nand_4_out;

  nand nand_1 (nand_1_out, s, e);
  nand nand_2 (nand_2_out, e, nand_1_out);
  nand nand_3 (q, nand_1_out, nand_4_out);
  nand nand_4 (nand_4_out, q, nand_2_out);

  // Notes on the sheet:
  //   1 bit memory cell
endmodule

module CPU_MEM_1 (
  input  s,
  input  e,
  output q
);

  wire nand_1_out, nand_2_out, nand_4_out;

  nand nand_1 (nand_1_out, s, e);
  nand nand_2 (nand_2_out, e, nand_1_out);
  nand nand_3 (q, nand_1_out, nand_4_out);
  nand nand_4 (nand_4_out, q, nand_2_out);

  // Notes on the sheet:
  //   1 bit memory cell
endmodule
